// Logisim project ETF.circ as structural Verilog: 116 circuits, main circuit REG1_LD
module ADD1 (
  input  Cin,
  input  A,
  input  B,
  output F,
  output Cout
);

  Adder #(.width(1)) adder_1 (.a(A), .b(B), .out(F), .cin(Cin), .cout(Cout));
endmodule

module ADD8 (
  input  C0,
  input  [7:0] A,
  input  [7:0] B,
  output [7:0] F,
  output C8
);

  Adder adder_1 (.a(A), .b(B), .out(F), .cin(C0), .cout(C8));
endmodule

module ADD9 (
  input  C0,
  input  [8:0] A,
  input  [8:0] B,
  output [8:0] F,
  output C9
);

  Adder #(.width(9)) adder_1 (.a(A), .b(B), .out(F), .cin(C0), .cout(C9));
endmodule

module ADD16 (
  input  C0,
  input  [15:0] A,
  input  [15:0] B,
  output [15:0] F,
  output C16
);

  Adder #(.width(16)) adder_1 (.a(A), .b(B), .out(F), .cin(C0), .cout(C16));
endmodule

module ALU1_ADD_SUB (
  input  Cin,
  input  A,
  input  B,
  input  add,
  input  sub,
  output F,
  output Cout
);

  wire adder_1_cout, adder_1_out, subtractor_1_bout, subtractor_1_out;

  Adder #(.width(1)) adder_1 (.a(A), .b(B), .out(adder_1_out), .cin(Cin), .cout(adder_1_cout));
  Subtractor #(.width(1)) subtractor_1 (.a(A), .b(B), .out(subtractor_1_out), .bin(Cin), .bout(subtractor_1_bout));
  assign F = add ? adder_1_out : 1'bz;  // Controlled_Buffer controlled_buffer_1
  assign Cout = add ? adder_1_cout : 1'bz;  // Controlled_Buffer controlled_buffer_2
  assign F = sub ? subtractor_1_out : 1'bz;  // Controlled_Buffer controlled_buffer_3
  assign Cout = sub ? subtractor_1_bout : 1'bz;  // Controlled_Buffer controlled_buffer_4
endmodule

module ALU1_ADD_SUB_AND_OR (
  input  Cin,
  input  A,
  input  B,
  input  add,
  input  sub,
  input  \and ,
  input  \or ,
  output F,
  output Cout
);

  wire adder_1_cout, adder_1_out, and_1_out, or_1_out, subtractor_1_bout, subtractor_1_out;

  Adder #(.width(1)) adder_1 (.a(A), .b(B), .out(adder_1_out), .cin(Cin), .cout(adder_1_cout));
  Subtractor #(.width(1)) subtractor_1 (.a(A), .b(B), .out(subtractor_1_out), .bin(Cin), .bout(subtractor_1_bout));
  and and_1 (and_1_out, A, B);
  or or_1 (or_1_out, A, B);
  assign F = add ? adder_1_out : 1'bz;  // Controlled_Buffer controlled_buffer_1
  assign Cout = add ? adder_1_cout : 1'bz;  // Controlled_Buffer controlled_buffer_2
  assign F = sub ? subtractor_1_out : 1'bz;  // Controlled_Buffer controlled_buffer_3
  assign Cout = sub ? subtractor_1_bout : 1'bz;  // Controlled_Buffer controlled_buffer_4
  assign F = \and  ? and_1_out : 1'bz;  // Controlled_Buffer controlled_buffer_5
  assign F = \or  ? or_1_out : 1'bz;  // Controlled_Buffer controlled_buffer_6
endmodule

module ALU8_ADD_SUB (
  input  Cin,
  input  [7:0] A,
  input  [7:0] B,
  input  add,
  input  sub,
  output [7:0] F,
  output Cout
);

  wire adder_1_cout, subtractor_1_bout;
  wire [7:0] adder_1_out, subtractor_1_out;

  Adder adder_1 (.a(A), .b(B), .out(adder_1_out), .cin(Cin), .cout(adder_1_cout));
  Subtractor subtractor_1 (.a(A), .b(B), .out(subtractor_1_out), .bin(Cin), .bout(subtractor_1_bout));
  assign F = add ? adder_1_out : 8'bz;  // Controlled_Buffer controlled_buffer_1
  assign Cout = add ? adder_1_cout : 1'bz;  // Controlled_Buffer controlled_buffer_2
  assign F = sub ? subtractor_1_out : 8'bz;  // Controlled_Buffer controlled_buffer_3
  assign Cout = sub ? subtractor_1_bout : 1'bz;  // Controlled_Buffer controlled_buffer_4
endmodule

module ALU8_ADD_SUB_AND_OR (
  input  Cin,
  input  [7:0] A,
  input  [7:0] B,
  input  add,
  input  sub,
  input  \and ,
  input  \or ,
  output [7:0] F,
  output Cout
);

  wire adder_1_cout, subtractor_1_bout;
  wire [7:0] adder_1_out, and_1_out, or_1_out, subtractor_1_out;

  Adder adder_1 (.a(A), .b(B), .out(adder_1_out), .cin(Cin), .cout(adder_1_cout));
  Subtractor subtractor_1 (.a(A), .b(B), .out(subtractor_1_out), .bin(Cin), .bout(subtractor_1_bout));
  assign and_1_out = A & B;  // AND_Gate and_1, 8 bits wide
  assign or_1_out = A | B;  // OR_Gate or_1, 8 bits wide
  assign F = add ? adder_1_out : 8'bz;  // Controlled_Buffer controlled_buffer_1
  assign Cout = add ? adder_1_cout : 1'bz;  // Controlled_Buffer controlled_buffer_2
  assign F = sub ? subtractor_1_out : 8'bz;  // Controlled_Buffer controlled_buffer_3
  assign Cout = sub ? subtractor_1_bout : 1'bz;  // Controlled_Buffer controlled_buffer_4
  assign F = \and  ? and_1_out : 8'bz;  // Controlled_Buffer controlled_buffer_5
  assign F = \or  ? or_1_out : 8'bz;  // Controlled_Buffer controlled_buffer_6
endmodule

module CD4 (
  input  En,
  input  C3,
  input  C2,
  input  C1,
  input  C0,
  output Z1,
  output Z0,
  output W
);

  wire or_1_out, or_2_out, or_3_out;

  Pull_Resistor #(.pull(1)) pull_resistor_1 (.node(En));
  or or_1 (or_1_out, C3, C2, C1, C0);
  or or_2 (or_2_out, C3, C2);
  or or_3 (or_3_out, C3, C1);
  and and_1 (Z1, En, or_2_out);
  and and_2 (Z0, En, or_3_out);
  and and_3 (W, En, or_1_out);

  // Notes on the sheet:
  //   uezti za podrazumevanu vrednost logičku jedinicu
  //   Ako En nije priključen (stanje visoke impednase - HiZ),
endmodule

module CD8 (
  input  En,
  input  C7,
  input  C6,
  input  C5,
  input  C4,
  input  C3,
  input  C2,
  input  C1,
  input  C0,
  output Z2,
  output Z1,
  output Z0,
  output W
);

  wire or_1_out, or_2_out, or_3_out, or_4_out;

  Pull_Resistor #(.pull(1)) pull_resistor_1 (.node(En));
  or or_1 (or_1_out, C7, C6, C5, C4, C3, C2, C1, C0);
  or or_2 (or_2_out, C7, C6, C5, C4);
  or or_3 (or_3_out, C7, C6, C3, C2);
  or or_4 (or_4_out, C7, C5, C3, C1);
  and and_1 (Z2, En, or_2_out);
  and and_2 (Z1, En, or_3_out);
  and and_3 (Z0, En, or_4_out);
  and and_4 (W, En, or_1_out);

  // Notes on the sheet:
  //   uezti za podrazumevanu vrednost logičku jedinicu
  //   Ako En nije priključen (stanje visoke impednase - HiZ),
endmodule

module DC1_2 (
  input  En,
  input  X0,
  output D0,
  output D1
);

  wire not_1_out;

  Pull_Resistor #(.pull(1)) pull_resistor_1 (.node(En));
  not not_1 (not_1_out, X0);
  and and_1 (D0, En, not_1_out);
  and and_2 (D1, En, X0);

  // Notes on the sheet:
  //   Ako En nije priključen (stanje visoke impednase - HiZ),
  //   uezti za podrazumevanu vrednost logičku jedinicu
endmodule

module DC2_4 (
  input  En,
  input  [1:0] X1__0,
  output D0,
  output D1,
  output D2,
  output D3
);

  wire dc1_2_1_d0, dc1_2_1_d1;

  Pull_Resistor #(.pull(1)) pull_resistor_1 (.node(En));
  DC1_2 dc1_2_1 (.En(En), .X0(X1__0[1]), .D0(dc1_2_1_d0), .D1(dc1_2_1_d1));
  DC1_2 dc1_2_2 (.En(dc1_2_1_d0), .X0(X1__0[0]), .D0(D0), .D1(D1));
  DC1_2 dc1_2_3 (.En(dc1_2_1_d1), .X0(X1__0[0]), .D0(D2), .D1(D3));

  // Notes on the sheet:
  //   Ako En nije priključen (stanje visoke impednase - HiZ),
  //   uezti za podrazumevanu vrednost logičku jedinicu
endmodule

module DC3_8 (
  input  En,
  input  [2:0] X2__0,
  output D0,
  output D1,
  output D2,
  output D3,
  output D4,
  output D5,
  output D6,
  output D7
);

  wire dc1_2_1_d0, dc1_2_1_d1;

  Pull_Resistor #(.pull(1)) pull_resistor_1 (.node(En));
  DC1_2 dc1_2_1 (.En(En), .X0(X2__0[2]), .D0(dc1_2_1_d0), .D1(dc1_2_1_d1));
  DC2_4 dc2_4_1 (.En(dc1_2_1_d0), .X1__0(X2__0[1:0]), .D0(D0), .D1(D1), .D2(D2), .D3(D3));
  DC2_4 dc2_4_2 (.En(dc1_2_1_d1), .X1__0(X2__0[1:0]), .D0(D4), .D1(D5), .D2(D6), .D3(D7));

  // Notes on the sheet:
  //   Ako En nije priključen (stanje visoke impednase - HiZ),
  //   uezti za podrazumevanu vrednost logičku jedinicu
endmodule

module DC4_16 (
  input  En,
  input  [3:0] X3__0,
  output D0,
  output D1,
  output D2,
  output D3,
  output D4,
  output D5,
  output D6,
  output D7,
  output D8,
  output D9,
  output D10,
  output D11,
  output D12,
  output D13,
  output D14,
  output D15
);

  wire dc1_2_1_d0, dc1_2_1_d1;

  Pull_Resistor #(.pull(1)) pull_resistor_1 (.node(En));
  DC1_2 dc1_2_1 (.En(En), .X0(X3__0[3]), .D0(dc1_2_1_d0), .D1(dc1_2_1_d1));
  DC3_8 dc3_8_1 (
    .En(dc1_2_1_d0), .X2__0(X3__0[2:0]), .D0(D0), .D1(D1), .D2(D2), .D3(D3), .D4(D4), .D5(D5), .D6(D6),
    .D7(D7));
  DC3_8 dc3_8_2 (
    .En(dc1_2_1_d1), .X2__0(X3__0[2:0]), .D0(D8), .D1(D9), .D2(D10), .D3(D11), .D4(D12), .D5(D13), .D6(D14),
    .D7(D15));

  // Notes on the sheet:
  //   Ako En nije priključen (stanje visoke impednase - HiZ),
  //   uezti za podrazumevanu vrednost logičku jedinicu
endmodule

module REG1 (
  input  CL,
  input  LD,
  input  I,
  input  SL,
  input  IL,
  input  SR,
  input  IR,
  input  INC,
  input  DEC,
  input  CLK,
  input  mr,
  output Cout,
  output Eout,
  output A
);

  wire and_1_out, and_2_out, and_3_out, and_4_out, and_5_out, and_6_out, and_7_out, and_8_out, and_9_out,
       and_10_out, or_1_out, or_2_out, rsff_1_notq;

  Pull_Resistor pull_resistor_1 (.node(CL));
  Pull_Resistor pull_resistor_2 (.node(LD));
  Pull_Resistor pull_resistor_3 (.node(I));
  Pull_Resistor pull_resistor_4 (.node(SL));
  Pull_Resistor pull_resistor_5 (.node(IL));
  Pull_Resistor pull_resistor_6 (.node(IR));
  Pull_Resistor pull_resistor_7 (.node(SR));
  Pull_Resistor pull_resistor_8 (.node(INC));
  Pull_Resistor pull_resistor_9 (.node(DEC));
  Pull_Resistor #(.pull(1)) pull_resistor_10 (.node(mr));
  and and_1 (and_1_out, LD, ~I);  // AND_Gate
  and and_2 (and_2_out, LD, I);
  and and_3 (and_3_out, SL, ~IL);  // AND_Gate
  and and_4 (and_4_out, SL, IL);
  and and_5 (and_5_out, SR, ~IR);  // AND_Gate
  and and_6 (and_6_out, SR, IR);
  and and_7 (and_7_out, A, INC);
  and and_8 (and_8_out, ~A, INC);  // AND_Gate
  and and_9 (and_9_out, A, DEC);
  and and_10 (and_10_out, ~A, DEC);  // AND_Gate
  or or_1 (or_1_out, and_10_out, and_8_out, and_6_out, and_4_out, and_2_out);
  or or_2 (or_2_out, and_9_out, and_7_out, and_5_out, and_3_out, and_1_out, CL);
  RSFF rsff_1 (.S(or_1_out), .CLK(CLK), .R(or_2_out), .Rd(mr), .Q(A), .notQ(rsff_1_notq));  // open: Sd
  and and_11 (Cout, A, INC);
  and and_12 (Eout, ~A, DEC);  // AND_Gate

  // Notes on the sheet:
  //   __
  //   Ako neka operacija (CL, LD, SL, SR, INC, DEC) nije priključen (stanje visoke impednase - HiZ),
  //   uezti za podrazumevanu vrednost logičku nulu
endmodule

module REG8 (
  input  CL,
  input  LD,
  input  [7:0] A,
  input  SL,
  input  IL,
  input  SR,
  input  IR,
  input  DEC,
  input  INC,
  input  mr,
  input  CLK,
  output Cout,
  output Eout,
  output [7:0] I
);

  wire reg1_2_cout, reg1_2_eout, reg1_3_cout, reg1_3_eout, reg1_4_cout, reg1_4_eout, reg1_5_cout,
       reg1_5_eout, reg1_6_cout, reg1_6_eout, reg1_7_cout, reg1_7_eout, reg1_8_cout, reg1_8_eout;

  REG1 reg1_1 (
    .CL(CL), .LD(LD), .I(A[7]), .SL(SL), .IL(I[6]), .SR(SR), .IR(IR), .CLK(CLK), .A(I[7]), .INC(reg1_2_cout),
    .DEC(reg1_2_eout), .Cout(Cout), .Eout(Eout), .mr(mr));
  REG1 reg1_2 (
    .CL(CL), .LD(LD), .I(A[6]), .SL(SL), .IL(I[5]), .SR(SR), .IR(I[7]), .CLK(CLK), .A(I[6]),
    .INC(reg1_3_cout), .DEC(reg1_3_eout), .Cout(reg1_2_cout), .Eout(reg1_2_eout), .mr(mr));
  REG1 reg1_3 (
    .CL(CL), .LD(LD), .I(A[5]), .SL(SL), .IL(I[4]), .SR(SR), .IR(I[6]), .CLK(CLK), .A(I[5]),
    .INC(reg1_4_cout), .DEC(reg1_4_eout), .Cout(reg1_3_cout), .Eout(reg1_3_eout), .mr(mr));
  REG1 reg1_4 (
    .CL(CL), .LD(LD), .I(A[4]), .SL(SL), .IL(I[3]), .SR(SR), .IR(I[5]), .CLK(CLK), .A(I[4]),
    .INC(reg1_5_cout), .DEC(reg1_5_eout), .Cout(reg1_4_cout), .Eout(reg1_4_eout), .mr(mr));
  REG1 reg1_5 (
    .CL(CL), .LD(LD), .I(A[3]), .SL(SL), .IL(I[2]), .SR(SR), .IR(I[4]), .CLK(CLK), .A(I[3]),
    .INC(reg1_6_cout), .DEC(reg1_6_eout), .Cout(reg1_5_cout), .Eout(reg1_5_eout), .mr(mr));
  REG1 reg1_6 (
    .CL(CL), .LD(LD), .I(A[2]), .SL(SL), .IL(I[1]), .SR(SR), .IR(I[3]), .CLK(CLK), .A(I[2]),
    .INC(reg1_7_cout), .DEC(reg1_7_eout), .Cout(reg1_6_cout), .Eout(reg1_6_eout), .mr(mr));
  REG1 reg1_7 (
    .CL(CL), .LD(LD), .I(A[1]), .SL(SL), .IL(I[0]), .SR(SR), .IR(I[2]), .CLK(CLK), .A(I[1]),
    .INC(reg1_8_cout), .DEC(reg1_8_eout), .Cout(reg1_7_cout), .Eout(reg1_7_eout), .mr(mr));
  REG1 reg1_8 (
    .CL(CL), .LD(LD), .I(A[0]), .SL(SL), .IL(IL), .SR(SR), .IR(I[1]), .CLK(CLK), .A(I[0]), .INC(INC),
    .DEC(DEC), .Cout(reg1_8_cout), .Eout(reg1_8_eout), .mr(mr));

  // Notes on the sheet:
  //   __
  //   7..0
  //   7..0
endmodule

module REG16 (
  input  CL,
  input  LD,
  input  [15:0] A,
  input  SL,
  input  IL,
  input  mr,
  input  SR,
  input  IR,
  input  DEC,
  input  INC,
  input  CLK,
  output Cout,
  output Eout,
  output [15:0] I
);

  wire reg8_2_cout, reg8_2_eout;

  REG8 reg8_1 (
    .CL(CL), .LD(LD), .A(A[15:8]), .SL(SL), .IL(I[7]), .SR(SR), .IR(IR), .DEC(reg8_2_eout),
    .INC(reg8_2_cout), .CLK(CLK), .I(I[15:8]), .Cout(Cout), .Eout(Eout), .mr(mr));
  REG8 reg8_2 (
    .CL(CL), .LD(LD), .A(A[7:0]), .SL(SL), .IL(IL), .SR(SR), .IR(I[8]), .DEC(DEC), .INC(INC), .CLK(CLK),
    .I(I[7:0]), .Cout(reg8_2_cout), .Eout(reg8_2_eout), .mr(mr));

  // Notes on the sheet:
  //   __
  //   15..0
  //   15..0
endmodule

module REG1_DEC_LD (
  input  I0,
  input  LD,
  input  DEC,
  input  mr,
  input  CLK,
  output A0
);

  REG1m_DEC_LD reg1m_dec_ld_1 (.Ii(I0), .LD(LD), .DEC(DEC), .Ei(DEC), .CLK(CLK), .Ai(A0), .mr(mr));  // open: Eout

  // Notes on the sheet:
  //   __
endmodule

module REG2_DEC_LD (
  input  [1:0] I1__0,
  input  LD,
  input  DEC,
  input  mr,
  input  CLK,
  output [1:0] A1__0
);

  REG2m_DEC_LD reg2m_dec_ld_1 (
    .I1__0(I1__0), .LD(LD), .Ein(DEC), .DEC(DEC), .CLK(CLK), .A1__0(A1__0), .mr(mr));  // open: Eout

  // Notes on the sheet:
  //   __
endmodule

module REG3_DEC_LD (
  input  [2:0] I2__0,
  input  LD,
  input  DEC,
  input  mr,
  input  CLK,
  output [2:0] A2__0
);

  wire reg1m_dec_ld_2_eout, reg1m_dec_ld_3_eout;

  REG1m_DEC_LD reg1m_dec_ld_1 (
    .Ii(I2__0[2]), .LD(LD), .DEC(DEC), .Ei(reg1m_dec_ld_2_eout), .CLK(CLK), .Ai(A2__0[2]), .mr(mr));  // open: Eout
  REG1m_DEC_LD reg1m_dec_ld_2 (
    .Ii(I2__0[1]), .LD(LD), .DEC(DEC), .Ei(reg1m_dec_ld_3_eout), .CLK(CLK), .Ai(A2__0[1]),
    .Eout(reg1m_dec_ld_2_eout), .mr(mr));
  REG1m_DEC_LD reg1m_dec_ld_3 (
    .Ii(I2__0[0]), .LD(LD), .DEC(DEC), .Ei(DEC), .CLK(CLK), .Ai(A2__0[0]), .Eout(reg1m_dec_ld_3_eout), .mr(mr));

  // Notes on the sheet:
  //   __
endmodule

module REG1_LD (
  input  Ii,
  input  LD,
  input  CLK,
  input  mr,
  output Ai
);

  wire and_1_out, and_2_out, or_1_out;

  Pull_Resistor pull_resistor_1 (.node(Ii));
  Pull_Resistor pull_resistor_2 (.node(LD));
  and and_1 (and_1_out, Ii, LD);
  and and_2 (and_2_out, ~LD, Ai);  // AND_Gate
  Pull_Resistor #(.pull(1)) pull_resistor_3 (.node(mr));
  or or_1 (or_1_out, and_1_out, and_2_out);
  DFF dff_1 (.CLK(CLK), .D(or_1_out), .Rd(mr), .Q(Ai));  // open: Sd, notQ

  // Notes on the sheet:
  //   __
endmodule

module REG2_LD (
  input  [1:0] I1__0,
  input  LD,
  input  mr,
  input  CLK,
  output [1:0] A1__0
);

  REG1_LD reg1_ld_1 (.Ii(I1__0[1]), .LD(LD), .CLK(CLK), .Ai(A1__0[1]), .mr(mr));
  REG1_LD reg1_ld_2 (.Ii(I1__0[0]), .LD(LD), .CLK(CLK), .Ai(A1__0[0]), .mr(mr));

  // Notes on the sheet:
  //   __
endmodule

module REG3_LD (
  input  [2:0] I2__0,
  input  LD,
  input  mr,
  input  CLK,
  output [2:0] A2__0
);

  REG1_LD reg1_ld_1 (.Ii(I2__0[2]), .LD(LD), .CLK(CLK), .Ai(A2__0[2]), .mr(mr));
  REG1_LD reg1_ld_2 (.Ii(I2__0[1]), .LD(LD), .CLK(CLK), .Ai(A2__0[1]), .mr(mr));
  REG1_LD reg1_ld_3 (.Ii(I2__0[0]), .LD(LD), .CLK(CLK), .Ai(A2__0[0]), .mr(mr));

  // Notes on the sheet:
  //   __
endmodule

module REG4_LD (
  input  [3:0] I3__0,
  input  LD,
  input  mr,
  input  CLK,
  output [3:0] A3__0
);

  REG2_LD reg2_ld_1 (.LD(LD), .CLK(CLK), .I1__0(I3__0[3:2]), .A1__0(A3__0[3:2]), .mr(mr));
  REG2_LD reg2_ld_2 (.LD(LD), .CLK(CLK), .I1__0(I3__0[1:0]), .A1__0(A3__0[1:0]), .mr(mr));

  // Notes on the sheet:
  //   __
endmodule

module REG8_LD (
  input  [7:0] I7__0,
  input  LD,
  input  mr,
  input  CLK,
  output [7:0] A7__0
);

  REG4_LD reg4_ld_1 (.I3__0(I7__0[7:4]), .LD(LD), .CLK(CLK), .A3__0(A7__0[7:4]), .mr(mr));
  REG4_LD reg4_ld_2 (.I3__0(I7__0[3:0]), .LD(LD), .CLK(CLK), .A3__0(A7__0[3:0]), .mr(mr));

  // Notes on the sheet:
  //   __
endmodule

module REG10_LD (
  input  [9:0] I9__0,
  input  LD,
  input  mr,
  input  CLK,
  output [9:0] A9__0
);

  REG2_LD reg2_ld_1 (.LD(LD), .CLK(CLK), .I1__0(I9__0[9:8]), .A1__0(A9__0[9:8]), .mr(mr));
  REG8_LD reg8_ld_1 (.I7__0(I9__0[7:0]), .LD(LD), .CLK(CLK), .A7__0(A9__0[7:0]), .mr(mr));

  // Notes on the sheet:
  //   __
endmodule

module REG16_LD (
  input  [15:0] I15__0,
  input  LD,
  input  mr,
  input  CLK,
  output [15:0] A15__0
);

  REG8_LD reg8_ld_1 (.I7__0(I15__0[15:8]), .LD(LD), .CLK(CLK), .A7__0(A15__0[15:8]), .mr(mr));
  REG8_LD reg8_ld_2 (.I7__0(I15__0[7:0]), .LD(LD), .CLK(CLK), .A7__0(A15__0[7:0]), .mr(mr));

  // Notes on the sheet:
  //   __
endmodule

module REG24_LD (
  input  [23:0] I23__0,
  input  LD,
  input  mr,
  input  CLK,
  output [23:0] A23__0
);

  REG8_LD reg8_ld_1 (.I7__0(I23__0[23:16]), .LD(LD), .CLK(CLK), .A7__0(A23__0[23:16]), .mr(mr));
  REG16_LD reg16_ld_1 (.I15__0(I23__0[15:0]), .LD(LD), .CLK(CLK), .A15__0(A23__0[15:0]), .mr(mr));

  // Notes on the sheet:
  //   __
endmodule

module REG1_LD_SR (
  input  Ii,
  input  LD,
  input  IR,
  input  SR,
  input  CLK,
  input  mr,
  output Ai
);

  wire and_1_out, and_2_out, and_3_out, or_1_out;

  Pull_Resistor pull_resistor_1 (.node(Ii));
  Pull_Resistor pull_resistor_2 (.node(LD));
  Pull_Resistor pull_resistor_3 (.node(SR));
  Pull_Resistor pull_resistor_4 (.node(IR));
  Pull_Resistor #(.pull(1)) pull_resistor_5 (.node(mr));
  and and_1 (and_1_out, IR, SR);
  and and_2 (and_2_out, Ii, LD);
  and and_3 (and_3_out, ~LD, ~SR, Ai);  // AND_Gate
  or or_1 (or_1_out, and_2_out, and_1_out, and_3_out);
  DFF dff_1 (.CLK(CLK), .D(or_1_out), .Rd(mr), .Q(Ai));  // open: Sd, notQ

  // Notes on the sheet:
  //   __
endmodule

module REG2_LD_SR (
  input  [1:0] I1__0,
  input  LD,
  input  IR,
  input  SR,
  input  mr,
  input  CLK,
  output [1:0] A1__0
);

  REG1_LD_SR reg1_ld_sr_1 (.Ii(I1__0[1]), .LD(LD), .IR(IR), .SR(SR), .CLK(CLK), .Ai(A1__0[1]), .mr(mr));
  REG1_LD_SR reg1_ld_sr_2 (.Ii(I1__0[0]), .LD(LD), .IR(A1__0[1]), .SR(SR), .CLK(CLK), .Ai(A1__0[0]), .mr(mr));

  // Notes on the sheet:
  //   __
endmodule

module REG3_LD_SR (
  input  [2:0] I2__0,
  input  LD,
  input  IR,
  input  SR,
  input  mr,
  input  CLK,
  output [2:0] A2__0
);

  REG1_LD_SR reg1_ld_sr_1 (.Ii(I2__0[2]), .LD(LD), .IR(IR), .SR(SR), .CLK(CLK), .Ai(A2__0[2]), .mr(mr));
  REG2_LD_SR reg2_ld_sr_1 (.I1__0(I2__0[1:0]), .LD(LD), .IR(A2__0[2]), .SR(SR), .CLK(CLK), .A1__0(A2__0[1:0]), .mr(mr));

  // Notes on the sheet:
  //   __
endmodule

module REG4_LD_SR (
  input  [3:0] I3__0,
  input  LD,
  input  IR,
  input  SR,
  input  mr,
  input  CLK,
  output [3:0] A3__0
);

  REG2_LD_SR reg2_ld_sr_1 (.I1__0(I3__0[3:2]), .LD(LD), .IR(IR), .SR(SR), .CLK(CLK), .A1__0(A3__0[3:2]), .mr(mr));
  REG2_LD_SR reg2_ld_sr_2 (.I1__0(I3__0[1:0]), .LD(LD), .IR(A3__0[2]), .SR(SR), .CLK(CLK), .A1__0(A3__0[1:0]), .mr(mr));

  // Notes on the sheet:
  //   __
endmodule

module REG8_LD_SR (
  input  [7:0] I7__0,
  input  LD,
  input  IR,
  input  SR,
  input  mr,
  input  CLK,
  output [7:0] A7__0
);

  REG4_LD_SR reg4_ld_sr_1 (.I3__0(I7__0[7:4]), .LD(LD), .IR(IR), .SR(SR), .CLK(CLK), .A3__0(A7__0[7:4]), .mr(mr));
  REG4_LD_SR reg4_ld_sr_2 (.I3__0(I7__0[3:0]), .LD(LD), .IR(A7__0[4]), .SR(SR), .CLK(CLK), .A3__0(A7__0[3:0]), .mr(mr));

  // Notes on the sheet:
  //   __
endmodule

module REG1_LD_SL_SR (
  input  Ii,
  input  LD,
  input  IR,
  input  SR,
  input  IL,
  input  SL,
  input  CLK,
  input  mr,
  output Ai
);

  wire and_1_out, and_2_out, and_3_out, and_4_out, or_1_out;

  Pull_Resistor pull_resistor_1 (.node(IR));
  Pull_Resistor pull_resistor_2 (.node(Ii));
  Pull_Resistor pull_resistor_3 (.node(SR));
  Pull_Resistor pull_resistor_4 (.node(SL));
  Pull_Resistor #(.pull(1)) pull_resistor_5 (.node(mr));
  Pull_Resistor pull_resistor_6 (.node(LD));
  Pull_Resistor pull_resistor_7 (.node(IL));
  and and_1 (and_1_out, Ii, LD);
  and and_2 (and_2_out, IR, SR);
  and and_3 (and_3_out, IL, SL);
  and and_4 (and_4_out, ~LD, ~SR, ~SL, Ai);  // AND_Gate
  or or_1 (or_1_out, and_1_out, and_2_out, and_3_out, and_4_out);
  DFF dff_1 (.CLK(CLK), .D(or_1_out), .Rd(mr), .Q(Ai));  // open: Sd, notQ

  // Notes on the sheet:
  //   __
endmodule

module REG2_LD_SL_SR (
  input  [1:0] I1__0,
  input  LD,
  input  IR,
  input  SR,
  input  IL,
  input  SL,
  input  mr,
  input  CLK,
  output [1:0] A1__0
);

  REG1_LD_SL_SR reg1_ld_sl_sr_1 (
    .Ii(I1__0[1]), .LD(LD), .IR(IR), .SR(SR), .IL(A1__0[0]), .SL(SL), .CLK(CLK), .Ai(A1__0[1]), .mr(mr));
  REG1_LD_SL_SR reg1_ld_sl_sr_2 (
    .Ii(I1__0[0]), .LD(LD), .IR(A1__0[1]), .SR(SR), .IL(IL), .SL(SL), .CLK(CLK), .Ai(A1__0[0]), .mr(mr));

  // Notes on the sheet:
  //   __
endmodule

module REG3_LD_SL_SR (
  input  [2:0] I2__0,
  input  LD,
  input  IR,
  input  SR,
  input  IL,
  input  SL,
  input  mr,
  input  CLK,
  output [2:0] A2__0
);

  REG1_LD_SL_SR reg1_ld_sl_sr_1 (
    .Ii(I2__0[2]), .LD(LD), .IR(IR), .SR(SR), .IL(A2__0[1]), .SL(SL), .CLK(CLK), .Ai(A2__0[2]), .mr(mr));
  REG2_LD_SL_SR reg2_ld_sl_sr_1 (
    .I1__0(I2__0[1:0]), .LD(LD), .IR(A2__0[2]), .SR(SR), .IL(IL), .SL(SL), .CLK(CLK), .A1__0(A2__0[1:0]),
    .mr(mr));

  // Notes on the sheet:
  //   __
endmodule

module REG4_LD_SL_SR (
  input  [3:0] I3__0,
  input  LD,
  input  IR,
  input  SR,
  input  IL,
  input  SL,
  input  mr,
  input  CLK,
  output [3:0] A3__0
);

  REG2_LD_SL_SR reg2_ld_sl_sr_1 (
    .I1__0(I3__0[3:2]), .LD(LD), .IR(IR), .SR(SR), .IL(A3__0[1]), .SL(SL), .CLK(CLK), .A1__0(A3__0[3:2]),
    .mr(mr));
  REG2_LD_SL_SR reg2_ld_sl_sr_2 (
    .I1__0(I3__0[1:0]), .LD(LD), .IR(A3__0[2]), .SR(SR), .IL(IL), .SL(SL), .CLK(CLK), .A1__0(A3__0[1:0]),
    .mr(mr));

  // Notes on the sheet:
  //   __
endmodule

module REG8_LD_SL_SR (
  input  [7:0] I7__0,
  input  LD,
  input  IR,
  input  SR,
  input  IL,
  input  SL,
  input  mr,
  input  CLK,
  output [7:0] A7__0
);

  REG4_LD_SL_SR reg4_ld_sl_sr_1 (
    .I3__0(I7__0[7:4]), .LD(LD), .IR(IR), .SR(SR), .IL(A7__0[3]), .SL(SL), .CLK(CLK), .A3__0(A7__0[7:4]),
    .mr(mr));
  REG4_LD_SL_SR reg4_ld_sl_sr_2 (
    .I3__0(I7__0[3:0]), .LD(LD), .IR(A7__0[4]), .SR(SR), .IL(IL), .SL(SL), .CLK(CLK), .A3__0(A7__0[3:0]),
    .mr(mr));

  // Notes on the sheet:
  //   __
endmodule

module REG1_CL_LD (
  input  Ii,
  input  LD,
  input  CL,
  input  CLK,
  input  mr,
  output Ai
);

  wire and_1_out, and_2_out, or_1_out;

  Pull_Resistor pull_resistor_1 (.node(LD));
  Pull_Resistor pull_resistor_2 (.node(CL));
  Pull_Resistor pull_resistor_3 (.node(Ii));
  Pull_Resistor #(.pull(1)) pull_resistor_4 (.node(mr));
  and and_1 (and_1_out, Ii, LD);
  and and_2 (and_2_out, ~LD, ~CL, Ai);  // AND_Gate
  or or_1 (or_1_out, and_1_out, and_2_out);
  DFF dff_1 (.CLK(CLK), .D(or_1_out), .Rd(mr), .Q(Ai));  // open: Sd, notQ

  // Notes on the sheet:
  //   __
endmodule

module REG2_CL_LD (
  input  [1:0] I1__0,
  input  CL,
  input  LD,
  input  mr,
  input  CLK,
  output [1:0] A1__0
);

  REG1_CL_LD reg1_cl_ld_1 (.CLK(CLK), .LD(LD), .CL(CL), .Ai(A1__0[1]), .Ii(I1__0[1]), .mr(mr));
  REG1_CL_LD reg1_cl_ld_2 (.CLK(CLK), .LD(LD), .CL(CL), .Ai(A1__0[0]), .Ii(I1__0[0]), .mr(mr));

  // Notes on the sheet:
  //   __
endmodule

module REG4_CL_LD (
  input  [3:0] I3__0,
  input  CL,
  input  LD,
  input  mr,
  input  CLK,
  output [3:0] A3__0
);

  REG2_CL_LD reg2_cl_ld_1 (.I1__0(I3__0[3:2]), .CL(CL), .LD(LD), .mr(mr), .CLK(CLK), .A1__0(A3__0[3:2]));
  REG2_CL_LD reg2_cl_ld_2 (.I1__0(I3__0[1:0]), .CL(CL), .LD(LD), .mr(mr), .CLK(CLK), .A1__0(A3__0[1:0]));

  // Notes on the sheet:
  //   __
endmodule

module REG8_CL_LD (
  input  [7:0] I7__0,
  input  CL,
  input  LD,
  input  mr,
  input  CLK,
  output [7:0] A7__0
);

  REG4_CL_LD reg4_cl_ld_1 (.I3__0(I7__0[7:4]), .CL(CL), .LD(LD), .mr(mr), .CLK(CLK), .A3__0(A7__0[7:4]));
  REG4_CL_LD reg4_cl_ld_2 (.I3__0(I7__0[3:0]), .CL(CL), .LD(LD), .mr(mr), .CLK(CLK), .A3__0(A7__0[3:0]));

  // Notes on the sheet:
  //   __
endmodule

module REG16_CL_LD (
  input  [15:0] I15__0,
  input  CL,
  input  LD,
  input  mr,
  input  CLK,
  output [15:0] A15__0
);

  REG8_CL_LD reg8_cl_ld_1 (.I7__0(I15__0[15:8]), .CL(CL), .LD(LD), .mr(mr), .CLK(CLK), .A7__0(A15__0[15:8]));
  REG8_CL_LD reg8_cl_ld_2 (.I7__0(I15__0[7:0]), .CL(CL), .LD(LD), .mr(mr), .CLK(CLK), .A7__0(A15__0[7:0]));

  // Notes on the sheet:
  //   __
endmodule

module REG1_CL_INC (
  input  CL,
  input  INC,
  input  mr,
  input  CLK,
  output A0
);

  REG1m_CL_INC reg1m_cl_inc_1 (.CL(CL), .INC(INC), .Ci(INC), .CLK(CLK), .Ai(A0), .mr(mr));  // open: Cout

  // Notes on the sheet:
  //   __
endmodule

module REG2_CL_INC (
  input  CL,
  input  INC,
  input  mr,
  input  CLK,
  output [1:0] A1__0
);

  REG2m_CL_INC reg2m_cl_inc_1 (.CL(CL), .Cin(INC), .INC(INC), .CLK(CLK), .A1__0(A1__0), .mr(mr));  // open: Cout

  // Notes on the sheet:
  //   __
endmodule

module REG3_CL_INC (
  input  CL,
  input  INC,
  input  mr,
  input  CLK,
  output [2:0] A2__0
);

  wire reg1m_cl_inc_2_cout, reg1m_cl_inc_3_cout;

  REG1m_CL_INC reg1m_cl_inc_1 (
    .CL(CL), .INC(INC), .Ci(reg1m_cl_inc_2_cout), .CLK(CLK), .Ai(A2__0[2]), .mr(mr));  // open: Cout
  REG1m_CL_INC reg1m_cl_inc_2 (
    .CL(CL), .INC(INC), .Ci(reg1m_cl_inc_3_cout), .CLK(CLK), .Ai(A2__0[1]), .Cout(reg1m_cl_inc_2_cout),
    .mr(mr));
  REG1m_CL_INC reg1m_cl_inc_3 (
    .CL(CL), .INC(INC), .Ci(INC), .CLK(CLK), .Ai(A2__0[0]), .Cout(reg1m_cl_inc_3_cout), .mr(mr));

  // Notes on the sheet:
  //   __
endmodule

module REG4_CL_INC (
  input  CL,
  input  INC,
  input  mr,
  input  CLK,
  output [3:0] A3__0
);

  wire reg2m_cl_inc_2_cout;

  REG2m_CL_INC reg2m_cl_inc_1 (
    .CL(CL), .Cin(reg2m_cl_inc_2_cout), .INC(INC), .CLK(CLK), .A1__0(A3__0[3:2]), .mr(mr));  // open: Cout
  REG2m_CL_INC reg2m_cl_inc_2 (
    .CL(CL), .Cin(INC), .INC(INC), .CLK(CLK), .Cout(reg2m_cl_inc_2_cout), .A1__0(A3__0[1:0]), .mr(mr));

  // Notes on the sheet:
  //   __
endmodule

module REG5_CL_INC (
  input  CL,
  input  INC,
  input  mr,
  input  CLK,
  output [4:0] A4__0
);

  wire reg4m_cl_inc_1_cout;

  REG1m_CL_INC reg1m_cl_inc_1 (
    .CL(CL), .INC(INC), .Ci(reg4m_cl_inc_1_cout), .CLK(CLK), .Ai(A4__0[4]), .mr(mr));  // open: Cout
  REG4m_CL_INC reg4m_cl_inc_1 (
    .CL(CL), .Cin(INC), .INC(INC), .CLK(CLK), .Cout(reg4m_cl_inc_1_cout), .A3__0(A4__0[3:0]), .mr(mr));

  // Notes on the sheet:
  //   __
endmodule

module REG1_CL_INC_LD (
  input  I0,
  input  LD,
  input  CL,
  input  INC,
  input  mr,
  input  CLK,
  output A0
);

  REG1m_CL_INC_LD reg1m_cl_inc_ld_1 (
    .Ii(I0), .LD(LD), .CL(CL), .INC(INC), .Ci(INC), .CLK(CLK), .Ai(A0), .mr(mr));  // open: Cout

  // Notes on the sheet:
  //   __
endmodule

module REG2_CL_INC_LD (
  input  [1:0] I1__0,
  input  LD,
  input  CL,
  input  INC,
  input  mr,
  input  CLK,
  output [1:0] A1__0
);

  REG2m_CL_INC_LD reg2m_cl_inc_ld_1 (
    .I1__0(I1__0), .LD(LD), .CL(CL), .Cin(INC), .INC(INC), .CLK(CLK), .A1__0(A1__0), .mr(mr));  // open: Cout

  // Notes on the sheet:
  //   __
endmodule

module REG3_CL_INC_LD (
  input  [2:0] I2__0,
  input  LD,
  input  CL,
  input  INC,
  input  mr,
  input  CLK,
  output [2:0] A2__0
);

  wire reg1m_cl_inc_ld_2_cout, reg1m_cl_inc_ld_3_cout;

  REG1m_CL_INC_LD reg1m_cl_inc_ld_1 (
    .Ii(I2__0[2]), .LD(LD), .CL(CL), .INC(INC), .Ci(reg1m_cl_inc_ld_2_cout), .CLK(CLK), .Ai(A2__0[2]), .mr(mr));  // open: Cout
  REG1m_CL_INC_LD reg1m_cl_inc_ld_2 (
    .Ii(I2__0[1]), .LD(LD), .CL(CL), .INC(INC), .Ci(reg1m_cl_inc_ld_3_cout), .CLK(CLK), .Ai(A2__0[1]),
    .Cout(reg1m_cl_inc_ld_2_cout), .mr(mr));
  REG1m_CL_INC_LD reg1m_cl_inc_ld_3 (
    .Ii(I2__0[0]), .LD(LD), .CL(CL), .INC(INC), .Ci(INC), .CLK(CLK), .Ai(A2__0[0]),
    .Cout(reg1m_cl_inc_ld_3_cout), .mr(mr));

  // Notes on the sheet:
  //   __
endmodule

module REG4_CL_INC_LD (
  input  [3:0] I3__0,
  input  LD,
  input  CL,
  input  INC,
  input  mr,
  input  CLK,
  output [3:0] A3__0
);

  wire reg2m_cl_inc_ld_2_cout;

  REG2m_CL_INC_LD reg2m_cl_inc_ld_1 (
    .I1__0(I3__0[3:2]), .LD(LD), .CL(CL), .Cin(reg2m_cl_inc_ld_2_cout), .INC(INC), .CLK(CLK),
    .A1__0(A3__0[3:2]), .mr(mr));  // open: Cout
  REG2m_CL_INC_LD reg2m_cl_inc_ld_2 (
    .I1__0(I3__0[1:0]), .LD(LD), .CL(CL), .Cin(INC), .INC(INC), .CLK(CLK), .Cout(reg2m_cl_inc_ld_2_cout),
    .A1__0(A3__0[1:0]), .mr(mr));

  // Notes on the sheet:
  //   __
endmodule

module REG5_CL_INC_LD (
  input  [4:0] I4__0,
  input  LD,
  input  CL,
  input  INC,
  input  mr,
  input  CLK,
  output [4:0] A4__0
);

  wire reg4m_cl_inc_ld_1_cout;

  REG1m_CL_INC_LD reg1m_cl_inc_ld_1 (
    .Ii(I4__0[4]), .LD(LD), .CL(CL), .INC(INC), .Ci(reg4m_cl_inc_ld_1_cout), .CLK(CLK), .Ai(A4__0[4]), .mr(mr));  // open: Cout
  REG4m_CL_INC_LD reg4m_cl_inc_ld_1 (
    .I3__0(I4__0[3:0]), .LD(LD), .CL(CL), .Cin(INC), .INC(INC), .CLK(CLK), .Cout(reg4m_cl_inc_ld_1_cout),
    .A3__0(A4__0[3:0]), .mr(mr));

  // Notes on the sheet:
  //   __
endmodule

module REG1_INC_LD (
  input  I0,
  input  LD,
  input  INC,
  input  mr,
  input  CLK,
  output A0
);

  REG1m_INC_LD reg1m_inc_ld_1 (.Ii(I0), .LD(LD), .INC(INC), .Ci(INC), .CLK(CLK), .Ai(A0), .mr(mr));  // open: Cout

  // Notes on the sheet:
  //   __
endmodule

module REG2_INC_LD (
  input  [1:0] I1__0,
  input  LD,
  input  INC,
  input  mr,
  input  CLK,
  output [1:0] A1__0
);

  REG2m_INC_LD reg2m_inc_ld_1 (
    .I1__0(I1__0), .LD(LD), .Cin(INC), .INC(INC), .CLK(CLK), .A1__0(A1__0), .mr(mr));  // open: Cout

  // Notes on the sheet:
  //   __
endmodule

module REG4_INC_LD (
  input  [3:0] I3__0,
  input  LD,
  input  INC,
  input  mr,
  input  CLK,
  output [3:0] A3__0
);

  REG4m_INC_LD reg4m_inc_ld_1 (
    .I3__0(I3__0), .LD(LD), .Cin(INC), .INC(INC), .CLK(CLK), .A3__0(A3__0), .mr(mr));  // open: Cout

  // Notes on the sheet:
  //   __
endmodule

module REG8_INC_LD (
  input  [7:0] I7__0,
  input  LD,
  input  INC,
  input  mr,
  input  CLK,
  output [7:0] A7__0
);

  REG8m_INC_LD reg8m_inc_ld_1 (
    .I7__0(I7__0), .LD(LD), .Cin(INC), .INC(INC), .mr(mr), .CLK(CLK), .A7__0(A7__0));  // open: Cout

  // Notes on the sheet:
  //   __
endmodule

module REG16_INC_LD (
  input  [15:0] I15__0,
  input  LD,
  input  INC,
  input  mr,
  input  CLK,
  output [15:0] A15__0
);

  REG16m_INC_LD reg16m_inc_ld_1 (
    .I15__0(I15__0), .LD(LD), .Cin(INC), .INC(INC), .mr(mr), .CLK(CLK), .A15__0(A15__0));  // open: Cout

  // Notes on the sheet:
  //   __
endmodule

module REG1_SR (
  input  IR,
  input  SR,
  input  CLK,
  input  mr,
  output Ai
);

  wire and_1_out, and_2_out, or_1_out;

  Pull_Resistor pull_resistor_1 (.node(IR));
  Pull_Resistor pull_resistor_2 (.node(SR));
  and and_1 (and_1_out, IR, SR);
  and and_2 (and_2_out, ~SR, Ai);  // AND_Gate
  Pull_Resistor #(.pull(1)) pull_resistor_3 (.node(mr));
  or or_1 (or_1_out, and_1_out, and_2_out);
  DFF dff_1 (.CLK(CLK), .D(or_1_out), .Rd(mr), .Q(Ai));  // open: Sd, notQ

  // Notes on the sheet:
  //   __
endmodule

module REG2_SR (
  input  IR,
  input  SR,
  input  mr,
  input  CLK,
  output [1:0] A1__0
);

  REG1_SR reg1_sr_1 (.IR(IR), .SR(SR), .CLK(CLK), .Ai(A1__0[1]), .mr(mr));
  REG1_SR reg1_sr_2 (.IR(A1__0[1]), .SR(SR), .CLK(CLK), .Ai(A1__0[0]), .mr(mr));

  // Notes on the sheet:
  //   __
endmodule

module REG3_SR (
  input  IR,
  input  SR,
  input  mr,
  input  CLK,
  output [2:0] A2__0
);

  REG1_SR reg1_sr_1 (.IR(IR), .SR(SR), .CLK(CLK), .Ai(A2__0[2]), .mr(mr));
  REG2_SR reg2_sr_1 (.IR(A2__0[2]), .SR(SR), .CLK(CLK), .A1__0(A2__0[1:0]), .mr(mr));

  // Notes on the sheet:
  //   __
endmodule

module REG4_SR (
  input  IR,
  input  SR,
  input  mr,
  input  CLK,
  output [3:0] A3__0
);

  REG2_SR reg2_sr_1 (.IR(IR), .SR(SR), .CLK(CLK), .A1__0(A3__0[3:2]), .mr(mr));
  REG2_SR reg2_sr_2 (.IR(A3__0[2]), .SR(SR), .CLK(CLK), .A1__0(A3__0[1:0]), .mr(mr));

  // Notes on the sheet:
  //   __
endmodule

module REG8_SR (
  input  IR,
  input  SR,
  input  mr,
  input  CLK,
  output [7:0] A7__0
);

  REG4_SR reg4_sr_1 (.IR(IR), .SR(SR), .CLK(CLK), .A3__0(A7__0[7:4]), .mr(mr));
  REG4_SR reg4_sr_2 (.IR(A7__0[4]), .SR(SR), .CLK(CLK), .A3__0(A7__0[3:0]), .mr(mr));

  // Notes on the sheet:
  //   __
endmodule

module REG1m_DEC_LD (
  input  Ii,
  input  LD,
  input  DEC,
  input  Ei,
  input  CLK,
  input  mr,
  output Ai,
  output Eout
);

  wire and_1_out, and_2_out, and_3_out, or_1_out, xor_1_out;

  Pull_Resistor pull_resistor_1 (.node(Ii));
  Pull_Resistor pull_resistor_2 (.node(Ei));
  Pull_Resistor pull_resistor_3 (.node(LD));
  xor xor_1 (xor_1_out, Ei, Ai);
  Pull_Resistor #(.pull(1)) pull_resistor_4 (.node(mr));
  Pull_Resistor pull_resistor_5 (.node(DEC));
  and and_1 (and_1_out, DEC, xor_1_out);
  and and_2 (and_2_out, Ii, LD);
  and and_3 (and_3_out, ~LD, ~DEC, Ai);  // AND_Gate
  or or_1 (or_1_out, and_2_out, and_3_out, and_1_out);
  DFF dff_1 (.CLK(CLK), .D(or_1_out), .Rd(mr), .Q(Ai));  // open: Sd, notQ
  and and_4 (Eout, ~Ai, Ei);  // AND_Gate

  // Notes on the sheet:
  //   __
endmodule

module REG2m_DEC_LD (
  input  [1:0] I1__0,
  input  LD,
  input  Ein,
  input  DEC,
  input  mr,
  input  CLK,
  output Eout,
  output [1:0] A1__0
);

  wire reg1m_dec_ld_2_eout;

  REG1m_DEC_LD reg1m_dec_ld_1 (
    .Ii(I1__0[1]), .LD(LD), .DEC(DEC), .Ei(reg1m_dec_ld_2_eout), .CLK(CLK), .Ai(A1__0[1]), .Eout(Eout),
    .mr(mr));
  REG1m_DEC_LD reg1m_dec_ld_2 (
    .Ii(I1__0[0]), .LD(LD), .DEC(DEC), .Ei(Ein), .CLK(CLK), .Ai(A1__0[0]), .Eout(reg1m_dec_ld_2_eout), .mr(mr));

  // Notes on the sheet:
  //   __
endmodule

module REG4m_DEC_LD (
  input  [3:0] I3__0,
  input  LD,
  input  Ein,
  input  DEC,
  input  mr,
  input  CLK,
  output Eout,
  output [3:0] A3__0
);

  wire reg2m_dec_ld_2_eout;

  REG2m_DEC_LD reg2m_dec_ld_1 (
    .I1__0(I3__0[3:2]), .LD(LD), .Ein(reg2m_dec_ld_2_eout), .DEC(DEC), .CLK(CLK), .Eout(Eout),
    .A1__0(A3__0[3:2]), .mr(mr));
  REG2m_DEC_LD reg2m_dec_ld_2 (
    .I1__0(I3__0[1:0]), .LD(LD), .Ein(Ein), .DEC(DEC), .CLK(CLK), .Eout(reg2m_dec_ld_2_eout),
    .A1__0(A3__0[1:0]), .mr(mr));

  // Notes on the sheet:
  //   __
endmodule

module REG1m_DEC_INC_LD (
  input  Ii,
  input  LD,
  input  DEC,
  input  Ei,
  input  INC,
  input  Ci,
  input  CLK,
  input  mr,
  output Ai,
  output Eout,
  output Cout
);

  wire and_1_out, and_2_out, and_3_out, and_4_out, or_1_out, xor_1_out, xor_2_out;

  Pull_Resistor pull_resistor_1 (.node(Ii));
  Pull_Resistor pull_resistor_2 (.node(Ei));
  Pull_Resistor pull_resistor_3 (.node(Ci));
  Pull_Resistor pull_resistor_4 (.node(INC));
  Pull_Resistor #(.pull(1)) pull_resistor_5 (.node(mr));
  Pull_Resistor pull_resistor_6 (.node(LD));
  Pull_Resistor pull_resistor_7 (.node(DEC));
  and and_1 (and_1_out, DEC, xor_1_out);
  xor xor_1 (xor_1_out, Ei, Ai);
  and and_2 (and_2_out, INC, xor_2_out);
  xor xor_2 (xor_2_out, Ci, Ai);
  and and_3 (and_3_out, Ii, LD);
  and and_4 (and_4_out, ~LD, ~DEC, ~INC, Ai);  // AND_Gate
  or or_1 (or_1_out, and_3_out, and_4_out, and_1_out, and_2_out);
  DFF dff_1 (.CLK(CLK), .D(or_1_out), .Rd(mr), .Q(Ai));  // open: Sd, notQ
  and and_5 (Eout, ~Ai, Ei);  // AND_Gate
  and and_6 (Cout, Ai, Ci);

  // Notes on the sheet:
  //   __
endmodule

module REG2m_DEC_INC_LD (
  input  [1:0] I1__0,
  input  LD,
  input  DEC,
  input  INC,
  input  mr,
  input  Ein,
  input  Cin,
  input  CLK,
  output Eout,
  output Cout,
  output [1:0] A1__0
);

  wire reg1m_dec_inc_ld_2_cout, reg1m_dec_inc_ld_2_eout;

  REG1m_DEC_INC_LD reg1m_dec_inc_ld_1 (
    .Ii(I1__0[1]), .LD(LD), .DEC(DEC), .Ei(reg1m_dec_inc_ld_2_eout), .INC(INC), .Ci(reg1m_dec_inc_ld_2_cout),
    .CLK(CLK), .mr(mr), .Ai(A1__0[1]), .Eout(Eout), .Cout(Cout));
  REG1m_DEC_INC_LD reg1m_dec_inc_ld_2 (
    .Ii(I1__0[0]), .LD(LD), .DEC(DEC), .Ei(Ein), .INC(INC), .Ci(Cin), .CLK(CLK), .mr(mr), .Ai(A1__0[0]),
    .Eout(reg1m_dec_inc_ld_2_eout), .Cout(reg1m_dec_inc_ld_2_cout));

  // Notes on the sheet:
  //   __
endmodule

module REG3m_DEC_INC_LD (
  input  [2:0] I2__0,
  input  LD,
  input  DEC,
  input  INC,
  input  mr,
  input  Ein,
  input  Cin,
  input  CLK,
  output Eout,
  output Cout,
  output [2:0] A2__0
);

  wire reg1m_dec_inc_ld_2_cout, reg1m_dec_inc_ld_2_eout, reg1m_dec_inc_ld_3_cout, reg1m_dec_inc_ld_3_eout;

  REG1m_DEC_INC_LD reg1m_dec_inc_ld_1 (
    .Ii(I2__0[2]), .LD(LD), .DEC(DEC), .Ei(reg1m_dec_inc_ld_2_eout), .INC(INC), .Ci(reg1m_dec_inc_ld_2_cout),
    .CLK(CLK), .mr(mr), .Ai(A2__0[2]), .Eout(Eout), .Cout(Cout));
  REG1m_DEC_INC_LD reg1m_dec_inc_ld_2 (
    .Ii(I2__0[1]), .LD(LD), .DEC(DEC), .Ei(reg1m_dec_inc_ld_3_eout), .INC(INC), .Ci(reg1m_dec_inc_ld_3_cout),
    .CLK(CLK), .mr(mr), .Ai(A2__0[1]), .Eout(reg1m_dec_inc_ld_2_eout), .Cout(reg1m_dec_inc_ld_2_cout));
  REG1m_DEC_INC_LD reg1m_dec_inc_ld_3 (
    .Ii(I2__0[0]), .LD(LD), .DEC(DEC), .Ei(Ein), .INC(INC), .Ci(Cin), .CLK(CLK), .mr(mr), .Ai(A2__0[0]),
    .Eout(reg1m_dec_inc_ld_3_eout), .Cout(reg1m_dec_inc_ld_3_cout));

  // Notes on the sheet:
  //   __
endmodule

module REG4m_DEC_INC_LD (
  input  [3:0] I3__0,
  input  LD,
  input  DEC,
  input  INC,
  input  mr,
  input  Ein,
  input  Cin,
  input  CLK,
  output Eout,
  output Cout,
  output [3:0] A3__0
);

  wire reg2m_dec_inc_ld_2_cout, reg2m_dec_inc_ld_2_eout;

  REG2m_DEC_INC_LD reg2m_dec_inc_ld_1 (
    .I1__0(I3__0[3:2]), .LD(LD), .DEC(DEC), .INC(INC), .mr(mr), .CLK(CLK), .Ein(reg2m_dec_inc_ld_2_eout),
    .Cin(reg2m_dec_inc_ld_2_cout), .Eout(Eout), .Cout(Cout), .A1__0(A3__0[3:2]));
  REG2m_DEC_INC_LD reg2m_dec_inc_ld_2 (
    .I1__0(I3__0[1:0]), .LD(LD), .DEC(DEC), .INC(INC), .mr(mr), .CLK(CLK), .Ein(Ein), .Cin(Cin),
    .Eout(reg2m_dec_inc_ld_2_eout), .Cout(reg2m_dec_inc_ld_2_cout), .A1__0(A3__0[1:0]));

  // Notes on the sheet:
  //   __
endmodule

module REG1m_CL_INC (
  input  CL,
  input  INC,
  input  Ci,
  input  CLK,
  input  mr,
  output Ai,
  output Cout
);

  wire and_1_out, and_2_out, or_1_out, xor_1_out;

  Pull_Resistor pull_resistor_1 (.node(CL));
  Pull_Resistor pull_resistor_2 (.node(INC));
  Pull_Resistor pull_resistor_3 (.node(Ci));
  xor xor_1 (xor_1_out, Ci, Ai);
  Pull_Resistor #(.pull(1)) pull_resistor_4 (.node(mr));
  and and_1 (and_1_out, INC, xor_1_out);
  and and_2 (and_2_out, ~CL, ~INC, Ai);  // AND_Gate
  or or_1 (or_1_out, and_2_out, and_1_out);
  DFF dff_1 (.CLK(CLK), .D(or_1_out), .Rd(mr), .Q(Ai));  // open: Sd, notQ
  and and_3 (Cout, Ai, Ci);

  // Notes on the sheet:
  //   __
endmodule

module REG2m_CL_INC (
  input  CL,
  input  Cin,
  input  INC,
  input  mr,
  input  CLK,
  output Cout,
  output [1:0] A1__0
);

  wire reg1m_cl_inc_2_cout;

  REG1m_CL_INC reg1m_cl_inc_1 (
    .CL(CL), .INC(INC), .Ci(reg1m_cl_inc_2_cout), .CLK(CLK), .Ai(A1__0[1]), .Cout(Cout), .mr(mr));
  REG1m_CL_INC reg1m_cl_inc_2 (
    .CL(CL), .INC(INC), .Ci(Cin), .CLK(CLK), .Ai(A1__0[0]), .Cout(reg1m_cl_inc_2_cout), .mr(mr));

  // Notes on the sheet:
  //   __
endmodule

module REG4m_CL_INC (
  input  CL,
  input  Cin,
  input  INC,
  input  mr,
  input  CLK,
  output Cout,
  output [3:0] A3__0
);

  wire reg2m_cl_inc_2_cout;

  REG2m_CL_INC reg2m_cl_inc_1 (
    .CL(CL), .Cin(reg2m_cl_inc_2_cout), .INC(INC), .CLK(CLK), .Cout(Cout), .A1__0(A3__0[3:2]), .mr(mr));
  REG2m_CL_INC reg2m_cl_inc_2 (
    .CL(CL), .Cin(Cin), .INC(INC), .CLK(CLK), .Cout(reg2m_cl_inc_2_cout), .A1__0(A3__0[1:0]), .mr(mr));

  // Notes on the sheet:
  //   __
endmodule

module REG1m_CL_INC_LD (
  input  Ii,
  input  LD,
  input  CL,
  input  INC,
  input  Ci,
  input  CLK,
  input  mr,
  output Ai,
  output Cout
);

  wire and_1_out, and_2_out, and_3_out, or_1_out, xor_1_out;

  Pull_Resistor pull_resistor_1 (.node(Ii));
  Pull_Resistor pull_resistor_2 (.node(Ci));
  Pull_Resistor pull_resistor_3 (.node(INC));
  Pull_Resistor pull_resistor_4 (.node(CL));
  Pull_Resistor pull_resistor_5 (.node(LD));
  xor xor_1 (xor_1_out, Ci, Ai);
  Pull_Resistor #(.pull(1)) pull_resistor_6 (.node(mr));
  and and_1 (and_1_out, INC, xor_1_out);
  and and_2 (and_2_out, Ii, LD);
  and and_3 (and_3_out, ~LD, ~CL, ~INC, Ai);  // AND_Gate
  or or_1 (or_1_out, and_2_out, and_3_out, and_1_out);
  DFF dff_1 (.CLK(CLK), .D(or_1_out), .Rd(mr), .Q(Ai));  // open: Sd, notQ
  and and_4 (Cout, Ai, Ci);

  // Notes on the sheet:
  //   __
endmodule

module REG2m_CL_INC_LD (
  input  [1:0] I1__0,
  input  LD,
  input  CL,
  input  Cin,
  input  INC,
  input  mr,
  input  CLK,
  output Cout,
  output [1:0] A1__0
);

  wire reg1m_cl_inc_ld_2_cout;

  REG1m_CL_INC_LD reg1m_cl_inc_ld_1 (
    .Ii(I1__0[1]), .LD(LD), .CL(CL), .INC(INC), .Ci(reg1m_cl_inc_ld_2_cout), .CLK(CLK), .Ai(A1__0[1]),
    .Cout(Cout), .mr(mr));
  REG1m_CL_INC_LD reg1m_cl_inc_ld_2 (
    .Ii(I1__0[0]), .LD(LD), .CL(CL), .INC(INC), .Ci(Cin), .CLK(CLK), .Ai(A1__0[0]),
    .Cout(reg1m_cl_inc_ld_2_cout), .mr(mr));

  // Notes on the sheet:
  //   __
endmodule

module REG4m_CL_INC_LD (
  input  [3:0] I3__0,
  input  LD,
  input  CL,
  input  Cin,
  input  INC,
  input  mr,
  input  CLK,
  output Cout,
  output [3:0] A3__0
);

  wire reg2m_cl_inc_ld_2_cout;

  REG2m_CL_INC_LD reg2m_cl_inc_ld_1 (
    .I1__0(I3__0[3:2]), .LD(LD), .CL(CL), .Cin(reg2m_cl_inc_ld_2_cout), .INC(INC), .CLK(CLK), .Cout(Cout),
    .A1__0(A3__0[3:2]), .mr(mr));
  REG2m_CL_INC_LD reg2m_cl_inc_ld_2 (
    .I1__0(I3__0[1:0]), .LD(LD), .CL(CL), .Cin(Cin), .INC(INC), .CLK(CLK), .Cout(reg2m_cl_inc_ld_2_cout),
    .A1__0(A3__0[1:0]), .mr(mr));

  // Notes on the sheet:
  //   __
endmodule

module REG1m_INC_LD (
  input  Ii,
  input  LD,
  input  INC,
  input  Ci,
  input  CLK,
  input  mr,
  output Ai,
  output Cout
);

  wire and_1_out, and_2_out, and_3_out, or_1_out, xor_1_out;

  Pull_Resistor pull_resistor_1 (.node(LD));
  Pull_Resistor pull_resistor_2 (.node(Ci));
  Pull_Resistor pull_resistor_3 (.node(Ii));
  Pull_Resistor pull_resistor_4 (.node(INC));
  Pull_Resistor #(.pull(1)) pull_resistor_5 (.node(mr));
  and and_1 (and_1_out, INC, xor_1_out);
  xor xor_1 (xor_1_out, Ci, Ai);
  and and_2 (and_2_out, Ii, LD);
  and and_3 (and_3_out, ~LD, ~INC, Ai);  // AND_Gate
  or or_1 (or_1_out, and_2_out, and_3_out, and_1_out);
  DFF dff_1 (.CLK(CLK), .D(or_1_out), .Rd(mr), .Q(Ai));  // open: Sd, notQ
  and and_4 (Cout, Ai, Ci);

  // Notes on the sheet:
  //   __
endmodule

module REG2m_INC_LD (
  input  [1:0] I1__0,
  input  LD,
  input  Cin,
  input  INC,
  input  mr,
  input  CLK,
  output Cout,
  output [1:0] A1__0
);

  wire reg1m_inc_ld_2_cout;

  REG1m_INC_LD reg1m_inc_ld_1 (
    .Ii(I1__0[1]), .LD(LD), .INC(INC), .Ci(reg1m_inc_ld_2_cout), .CLK(CLK), .Ai(A1__0[1]), .Cout(Cout),
    .mr(mr));
  REG1m_INC_LD reg1m_inc_ld_2 (
    .Ii(I1__0[0]), .LD(LD), .INC(INC), .Ci(Cin), .CLK(CLK), .Ai(A1__0[0]), .Cout(reg1m_inc_ld_2_cout), .mr(mr));

  // Notes on the sheet:
  //   __
endmodule

module REG4m_INC_LD (
  input  [3:0] I3__0,
  input  LD,
  input  Cin,
  input  INC,
  input  mr,
  input  CLK,
  output Cout,
  output [3:0] A3__0
);

  wire reg2m_inc_ld_2_cout;

  REG2m_INC_LD reg2m_inc_ld_1 (
    .I1__0(I3__0[3:2]), .LD(LD), .Cin(reg2m_inc_ld_2_cout), .INC(INC), .CLK(CLK), .Cout(Cout),
    .A1__0(A3__0[3:2]), .mr(mr));
  REG2m_INC_LD reg2m_inc_ld_2 (
    .I1__0(I3__0[1:0]), .LD(LD), .Cin(Cin), .INC(INC), .CLK(CLK), .Cout(reg2m_inc_ld_2_cout),
    .A1__0(A3__0[1:0]), .mr(mr));

  // Notes on the sheet:
  //   __
endmodule

module REG8m_INC_LD (
  input  [7:0] I7__0,
  input  LD,
  input  Cin,
  input  INC,
  input  mr,
  input  CLK,
  output Cout,
  output [7:0] A7__0
);

  wire reg4m_inc_ld_2_cout;

  REG4m_INC_LD reg4m_inc_ld_1 (
    .I3__0(I7__0[7:4]), .LD(LD), .Cin(reg4m_inc_ld_2_cout), .INC(INC), .CLK(CLK), .Cout(Cout),
    .A3__0(A7__0[7:4]), .mr(mr));
  REG4m_INC_LD reg4m_inc_ld_2 (
    .I3__0(I7__0[3:0]), .LD(LD), .Cin(Cin), .INC(INC), .CLK(CLK), .Cout(reg4m_inc_ld_2_cout),
    .A3__0(A7__0[3:0]), .mr(mr));

  // Notes on the sheet:
  //   __
endmodule

module REG16m_INC_LD (
  input  [15:0] I15__0,
  input  LD,
  input  Cin,
  input  INC,
  input  mr,
  input  CLK,
  output Cout,
  output [15:0] A15__0
);

  wire reg8m_inc_ld_2_cout;

  REG8m_INC_LD reg8m_inc_ld_1 (
    .I7__0(I15__0[15:8]), .LD(LD), .Cin(reg8m_inc_ld_2_cout), .INC(INC), .mr(mr), .CLK(CLK), .Cout(Cout),
    .A7__0(A15__0[15:8]));
  REG8m_INC_LD reg8m_inc_ld_2 (
    .I7__0(I15__0[7:0]), .LD(LD), .Cin(Cin), .INC(INC), .mr(mr), .CLK(CLK), .Cout(reg8m_inc_ld_2_cout),
    .A7__0(A15__0[7:0]));

  // Notes on the sheet:
  //   __
endmodule

module RisingEdge (
  input  INPUT,
  input  CLK,
  output OUTPUT
);

  wire dff_1_q, dff_2_q;

  DFF dff_1 (.CLK(CLK), .D(INPUT), .Q(dff_1_q));  // open: Sd, Rd, notQ
  DFF dff_2 (.CLK(CLK), .D(dff_1_q), .Q(dff_2_q));  // open: Sd, Rd, notQ
  and and_1 (OUTPUT, dff_1_q, ~dff_2_q);  // AND_Gate
endmodule

module FallingEdge (
  input  INPUT,
  input  CLK,
  output OUTPUT
);

  wire dff_1_q, dff_2_q;

  DFF dff_1 (.CLK(CLK), .D(INPUT), .Q(dff_1_q));  // open: Sd, Rd, notQ
  DFF dff_2 (.CLK(CLK), .D(dff_1_q), .Q(dff_2_q));  // open: Sd, Rd, notQ
  and and_1 (OUTPUT, ~dff_1_q, dff_2_q);  // AND_Gate
endmodule

module MP2_1b (
  input  En,
  input  I0,
  input  I1,
  input  S0,
  output Y
);

  wire and_1_out, and_2_out, not_1_out, or_1_out;

  Pull_Resistor #(.pull(1)) pull_resistor_1 (.node(En));
  not not_1 (not_1_out, S0);
  and and_1 (and_1_out, I0, not_1_out);
  and and_2 (and_2_out, I1, S0);
  or or_1 (or_1_out, and_1_out, and_2_out);
  and and_3 (Y, En, or_1_out);

  // Notes on the sheet:
  //   Ako En nije priključen (stanje visoke impednase - HiZ),
  //   uezti za podrazumevanu vrednost logičku jedinicu
endmodule

module MP2_4b (
  input  En,
  input  [3:0] in_2,
  input  [3:0] in_3,
  input  S0,
  output [3:0] Y
);

  wire not_1_out;
  wire [3:0] and_1_out, and_2_out, bit_extender_1_out, bit_extender_2_out, bit_extender_3_out, or_1_out;

  Pull_Resistor #(.pull(1)) pull_resistor_1 (.node(En));
  assign bit_extender_1_out = {{3{S0}}, S0};  // Bit_Extender bit_extender_1
  not not_1 (not_1_out, S0);
  assign bit_extender_2_out = {{3{not_1_out}}, not_1_out};  // Bit_Extender bit_extender_2
  assign and_1_out = in_2 & bit_extender_2_out;  // AND_Gate and_1, 4 bits wide
  assign and_2_out = in_3 & bit_extender_1_out;  // AND_Gate and_2, 4 bits wide
  assign bit_extender_3_out = {{3{En}}, En};  // Bit_Extender bit_extender_3
  assign or_1_out = and_1_out | and_2_out;  // OR_Gate or_1, 4 bits wide
  assign Y = bit_extender_3_out & or_1_out;  // AND_Gate and_3, 4 bits wide

  // Notes on the sheet:
  //   I0
  //   3..0
  //   I1
  //   3..0
  //   Ako En nije priključen (stanje visoke impednase - HiZ),
  //   uezti za podrazumevanu vrednost logičku jedinicu
  //   3..0
endmodule

module MP2_8b (
  input  En,
  input  [7:0] in_2,
  input  [7:0] in_3,
  input  S0,
  output [7:0] out_5
);

  wire not_1_out;
  wire [7:0] and_1_out, and_2_out, bit_extender_1_out, bit_extender_2_out, bit_extender_3_out, or_1_out;

  Pull_Resistor #(.pull(1)) pull_resistor_1 (.node(En));
  assign bit_extender_1_out = {{7{S0}}, S0};  // Bit_Extender bit_extender_1
  not not_1 (not_1_out, S0);
  assign bit_extender_2_out = {{7{not_1_out}}, not_1_out};  // Bit_Extender bit_extender_2
  assign and_1_out = in_2 & bit_extender_2_out;  // AND_Gate and_1, 8 bits wide
  assign and_2_out = in_3 & bit_extender_1_out;  // AND_Gate and_2, 8 bits wide
  assign bit_extender_3_out = {{7{En}}, En};  // Bit_Extender bit_extender_3
  assign or_1_out = and_1_out | and_2_out;  // OR_Gate or_1, 8 bits wide
  assign out_5 = bit_extender_3_out & or_1_out;  // AND_Gate and_3, 8 bits wide

  // Notes on the sheet:
  //   I0
  //   7..0
  //   I1
  //   7..0
  //   Ako En nije priključen (stanje visoke impednase - HiZ),
  //   uezti za podrazumevanu vrednost logičku jedinicu
  //   Y
  //   7..0
endmodule

module MP2_16b (
  input  En,
  input  [15:0] in_2,
  input  [15:0] in_3,
  input  S0,
  output [15:0] out_5
);

  wire not_1_out;
  wire [15:0] and_1_out, and_2_out, bit_extender_1_out, bit_extender_2_out, bit_extender_3_out, or_1_out;

  Pull_Resistor #(.pull(1)) pull_resistor_1 (.node(En));
  assign bit_extender_1_out = {{15{S0}}, S0};  // Bit_Extender bit_extender_1
  assign bit_extender_2_out = {{15{not_1_out}}, not_1_out};  // Bit_Extender bit_extender_2
  not not_1 (not_1_out, S0);
  assign and_1_out = in_2 & bit_extender_2_out;  // AND_Gate and_1, 16 bits wide
  assign and_2_out = in_3 & bit_extender_1_out;  // AND_Gate and_2, 16 bits wide
  assign bit_extender_3_out = {{15{En}}, En};  // Bit_Extender bit_extender_3
  assign or_1_out = and_1_out | and_2_out;  // OR_Gate or_1, 16 bits wide
  assign out_5 = bit_extender_3_out & or_1_out;  // AND_Gate and_3, 16 bits wide

  // Notes on the sheet:
  //   I0
  //   15..0
  //   I1
  //   15..0
  //   Ako En nije priključen (stanje visoke impednase - HiZ),
  //   uezti za podrazumevanu vrednost logičku jedinicu
  //   Y
  //   15..0
endmodule

module MP4_1b (
  input  I0,
  input  I1,
  input  I2,
  input  I3,
  input  En,
  input  S0,
  input  S1,
  output Y
);

  wire mp2_1b_1_y, mp2_1b_3_y;

  MP2_1b mp2_1b_1 (.I0(I0), .I1(I1), .S0(S0), .Y(mp2_1b_1_y));  // open: En
  MP2_1b mp2_1b_2 (.I0(mp2_1b_1_y), .I1(mp2_1b_3_y), .S0(S1), .Y(Y), .En(En));
  MP2_1b mp2_1b_3 (.I0(I2), .I1(I3), .S0(S0), .Y(mp2_1b_3_y));  // open: En
endmodule

module MP4_4b (
  input  [3:0] I0,
  input  [3:0] I1,
  input  [3:0] I2,
  input  [3:0] I3,
  input  En,
  input  S0,
  input  S1,
  output [3:0] Y
);

  wire [3:0] mp2_4b_1_y, mp2_4b_3_y;

  Pull_Resistor #(.pull(1)) pull_resistor_1 (.node(En));
  MP2_4b mp2_4b_1 (.in_2(I0), .in_3(I1), .S0(S0), .Y(mp2_4b_1_y));  // open: En
  MP2_4b mp2_4b_2 (.En(En), .in_2(mp2_4b_1_y), .in_3(mp2_4b_3_y), .S0(S1), .Y(Y));
  MP2_4b mp2_4b_3 (.in_2(I2), .in_3(I3), .S0(S0), .Y(mp2_4b_3_y));  // open: En

  // Notes on the sheet:
  //   Ako En nije priključen (stanje visoke impednase - HiZ),
  //   uezti za podrazumevanu vrednost logičku jedinicu
  //   3..0
  //   3..0
  //   3..0
  //   3..0
endmodule

module MP4_8b (
  input  [7:0] I0,
  input  [7:0] I1,
  input  [7:0] I2,
  input  [7:0] I3,
  input  En,
  input  S0,
  input  S1,
  output [7:0] Y
);

  wire [7:0] mp2_8b_1_out_5, mp2_8b_3_out_5;

  Pull_Resistor #(.pull(1)) pull_resistor_1 (.node(En));
  MP2_8b mp2_8b_1 (.in_2(I0), .in_3(I1), .S0(S0), .out_5(mp2_8b_1_out_5));  // open: En
  MP2_8b mp2_8b_2 (.in_2(mp2_8b_1_out_5), .in_3(mp2_8b_3_out_5), .S0(S1), .out_5(Y), .En(En));
  MP2_8b mp2_8b_3 (.in_2(I2), .in_3(I3), .S0(S0), .out_5(mp2_8b_3_out_5));  // open: En

  // Notes on the sheet:
  //   Ako En nije priključen (stanje visoke impednase - HiZ),
  //   uezti za podrazumevanu vrednost logičku jedinicu
  //   7..0
  //   7..0
  //   7..0
  //   7..0
endmodule

module MP4_16b (
  input  [15:0] I0,
  input  [15:0] I1,
  input  [15:0] I2,
  input  [15:0] I3,
  input  En,
  input  S0,
  input  S1,
  output [15:0] Y
);

  wire [15:0] mp2_16b_1_out_5, mp2_16b_3_out_5;

  Pull_Resistor #(.pull(1)) pull_resistor_1 (.node(En));
  MP2_16b mp2_16b_1 (.in_2(I0), .in_3(I1), .S0(S0), .out_5(mp2_16b_1_out_5));  // open: En
  MP2_16b mp2_16b_2 (.En(En), .in_2(mp2_16b_1_out_5), .in_3(mp2_16b_3_out_5), .S0(S1), .out_5(Y));
  MP2_16b mp2_16b_3 (.in_2(I2), .in_3(I3), .S0(S0), .out_5(mp2_16b_3_out_5));  // open: En

  // Notes on the sheet:
  //   Ako En nije priključen (stanje visoke impednase - HiZ),
  //   uezti za podrazumevanu vrednost logičku jedinicu
  //   15..0
  //   15..0
  //   15..0
  //   15..0
endmodule

module MP8_1b (
  input  I0,
  input  I1,
  input  I2,
  input  I3,
  input  I4,
  input  I5,
  input  I6,
  input  I7,
  input  En,
  input  S0,
  input  S1,
  input  S2,
  output Y
);

  wire mp2_1b_1_y, mp2_1b_2_y, mp2_1b_3_y, mp2_1b_5_y, mp2_1b_6_y, mp2_1b_7_y;

  MP2_1b mp2_1b_1 (.I0(I0), .I1(I1), .S0(S0), .Y(mp2_1b_1_y));  // open: En
  MP2_1b mp2_1b_2 (.I0(mp2_1b_1_y), .I1(mp2_1b_3_y), .S0(S1), .Y(mp2_1b_2_y), .En(En));
  MP2_1b mp2_1b_3 (.I0(I2), .I1(I3), .S0(S0), .Y(mp2_1b_3_y));  // open: En
  MP2_1b mp2_1b_4 (.I0(mp2_1b_2_y), .I1(mp2_1b_6_y), .S0(S2), .Y(Y), .En(En));
  MP2_1b mp2_1b_5 (.I0(I4), .I1(I5), .S0(S0), .Y(mp2_1b_5_y));  // open: En
  MP2_1b mp2_1b_6 (.I0(mp2_1b_5_y), .I1(mp2_1b_7_y), .S0(S1), .Y(mp2_1b_6_y), .En(En));
  MP2_1b mp2_1b_7 (.I0(I6), .I1(I7), .S0(S0), .Y(mp2_1b_7_y));  // open: En
endmodule

module MP8_4b (
  input  [3:0] I0,
  input  [3:0] I1,
  input  [3:0] I2,
  input  [3:0] I3,
  input  [3:0] I4,
  input  [3:0] I5,
  input  [3:0] I6,
  input  [3:0] I7,
  input  En,
  input  S0,
  input  S1,
  input  S2,
  output [3:0] Y
);

  wire [3:0] mp2_4b_1_y, mp2_4b_2_y, mp2_4b_3_y, mp2_4b_5_y, mp2_4b_6_y, mp2_4b_7_y;

  MP2_4b mp2_4b_1 (.in_2(I0), .in_3(I1), .S0(S0), .Y(mp2_4b_1_y));  // open: En
  MP2_4b mp2_4b_2 (.in_2(mp2_4b_1_y), .in_3(mp2_4b_3_y), .S0(S1), .Y(mp2_4b_2_y));  // open: En
  MP2_4b mp2_4b_3 (.in_2(I2), .in_3(I3), .S0(S0), .Y(mp2_4b_3_y));  // open: En
  MP2_4b mp2_4b_4 (.En(En), .in_2(mp2_4b_2_y), .in_3(mp2_4b_6_y), .S0(S2), .Y(Y));
  MP2_4b mp2_4b_5 (.in_2(I4), .in_3(I5), .S0(S0), .Y(mp2_4b_5_y));  // open: En
  MP2_4b mp2_4b_6 (.in_2(mp2_4b_5_y), .in_3(mp2_4b_7_y), .S0(S1), .Y(mp2_4b_6_y));  // open: En
  MP2_4b mp2_4b_7 (.in_2(I6), .in_3(I7), .S0(S0), .Y(mp2_4b_7_y));  // open: En
endmodule

module MP8_8b (
  input  [7:0] I0,
  input  [7:0] I1,
  input  [7:0] I2,
  input  [7:0] I3,
  input  [7:0] I4,
  input  [7:0] I5,
  input  [7:0] I6,
  input  [7:0] I7,
  input  En,
  input  S0,
  input  S1,
  input  S2,
  output [7:0] Y
);

  wire [7:0] mp2_8b_1_out_5, mp2_8b_2_out_5, mp2_8b_3_out_5, mp2_8b_5_out_5, mp2_8b_6_out_5, mp2_8b_7_out_5;

  MP2_8b mp2_8b_1 (.in_2(I0), .in_3(I1), .S0(S0), .out_5(mp2_8b_1_out_5));  // open: En
  MP2_8b mp2_8b_2 (.in_2(mp2_8b_1_out_5), .in_3(mp2_8b_3_out_5), .S0(S1), .out_5(mp2_8b_2_out_5));  // open: En
  MP2_8b mp2_8b_3 (.in_2(I2), .in_3(I3), .S0(S0), .out_5(mp2_8b_3_out_5));  // open: En
  MP2_8b mp2_8b_4 (.in_2(mp2_8b_2_out_5), .in_3(mp2_8b_6_out_5), .S0(S2), .out_5(Y), .En(En));
  MP2_8b mp2_8b_5 (.in_2(I4), .in_3(I5), .S0(S0), .out_5(mp2_8b_5_out_5));  // open: En
  MP2_8b mp2_8b_6 (.in_2(mp2_8b_5_out_5), .in_3(mp2_8b_7_out_5), .S0(S1), .out_5(mp2_8b_6_out_5));  // open: En
  MP2_8b mp2_8b_7 (.in_2(I6), .in_3(I7), .S0(S0), .out_5(mp2_8b_7_out_5));  // open: En
endmodule

module MP8_16b (
  input  [15:0] I0,
  input  [15:0] I1,
  input  [15:0] I2,
  input  [15:0] I3,
  input  [15:0] I4,
  input  [15:0] I5,
  input  [15:0] I6,
  input  [15:0] I7,
  input  En,
  input  S0,
  input  S1,
  input  S2,
  output [15:0] Y
);

  wire [15:0] mp2_16b_1_out_5, mp2_16b_2_out_5, mp2_16b_3_out_5, mp2_16b_5_out_5, mp2_16b_6_out_5,
       mp2_16b_7_out_5;

  MP2_16b mp2_16b_1 (.in_2(I0), .in_3(I1), .S0(S0), .out_5(mp2_16b_1_out_5));  // open: En
  MP2_16b mp2_16b_2 (.in_2(mp2_16b_1_out_5), .in_3(mp2_16b_3_out_5), .S0(S1), .out_5(mp2_16b_2_out_5));  // open: En
  MP2_16b mp2_16b_3 (.in_2(I2), .in_3(I3), .S0(S0), .out_5(mp2_16b_3_out_5));  // open: En
  MP2_16b mp2_16b_4 (.En(En), .in_2(mp2_16b_2_out_5), .in_3(mp2_16b_6_out_5), .S0(S2), .out_5(Y));
  MP2_16b mp2_16b_5 (.in_2(I4), .in_3(I5), .S0(S0), .out_5(mp2_16b_5_out_5));  // open: En
  MP2_16b mp2_16b_6 (.in_2(mp2_16b_5_out_5), .in_3(mp2_16b_7_out_5), .S0(S1), .out_5(mp2_16b_6_out_5));  // open: En
  MP2_16b mp2_16b_7 (.in_2(I6), .in_3(I7), .S0(S0), .out_5(mp2_16b_7_out_5));  // open: En
endmodule

module DFF (
  input  CLK,
  input  D,
  input  Sd,
  input  Rd,
  output Q,
  output notQ
);

  wire not_1_out, not_2_out;

  not not_1 (not_1_out, Sd);
  not not_2 (not_2_out, Rd);
  D_Flip_Flop d_ff_1 (.clk(CLK), .D(D), .Q(Q), .Qn(notQ), .preset(not_1_out), .reset(not_2_out));  // open: en
endmodule

module TFF (
  input  CLK,
  input  T,
  input  Sd,
  input  Rd,
  output Q,
  output notQ
);

  wire not_1_out, not_2_out;

  not not_1 (not_1_out, Sd);
  not not_2 (not_2_out, Rd);
  T_Flip_Flop t_ff_1 (.clk(CLK), .T(T), .Q(Q), .Qn(notQ), .preset(not_1_out), .reset(not_2_out));  // open: en
endmodule

module RSFF (
  input  S,
  input  CLK,
  input  R,
  input  Sd,
  input  Rd,
  output Q,
  output notQ
);

  wire not_1_out, not_2_out;

  not not_1 (not_1_out, Sd);
  not not_2 (not_2_out, Rd);
  S_R_Flip_Flop s_r_ff_1 (
    .S(S), .clk(CLK), .R(R), .Q(Q), .Qn(notQ), .preset(not_1_out), .reset(not_2_out));  // open: en
endmodule

module JKFF (
  input  J,
  input  CLK,
  input  K,
  input  Sd,
  input  Rd,
  output Q,
  output notQ
);

  wire not_1_out, not_2_out;

  not not_1 (not_1_out, Sd);
  not not_2 (not_2_out, Rd);
  J_K_Flip_Flop j_k_ff_1 (
    .J(J), .clk(CLK), .K(K), .Q(Q), .Qn(notQ), .preset(not_1_out), .reset(not_2_out));  // open: en
endmodule

module SUB1 (
  input  Ein,
  input  A,
  input  B,
  output F,
  output Eout
);

  Subtractor #(.width(1)) subtractor_1 (.a(A), .b(B), .out(F), .bin(Ein), .bout(Eout));
endmodule

module SUB8 (
  input  E0,
  input  [7:0] A,
  input  [7:0] B,
  output [7:0] F,
  output E8
);

  Subtractor subtractor_1 (.a(A), .b(B), .out(F), .bin(E0), .bout(E8));
endmodule

module SUB16 (
  input  E0,
  input  [15:0] A,
  input  [15:0] B,
  output [15:0] F,
  output E16
);

  Subtractor #(.width(16)) subtractor_1 (.a(A), .b(B), .out(F), .bin(E0), .bout(E16));
endmodule

module INC1 (
  input  Cin,
  input  A,
  output F,
  output Cout
);

  xor xor_1 (F, Cin, A);
  and and_1 (Cout, Cin, A);
endmodule

module INC8 (
  input  [7:0] A,
  input  Cin,
  output Cout,
  output [7:0] F
);

  wire inc1_2_cout, inc1_3_cout, inc1_4_cout, inc1_5_cout, inc1_6_cout, inc1_7_cout, inc1_8_cout;

  INC1 inc1_1 (.Cin(inc1_2_cout), .A(A[7]), .F(F[7]), .Cout(Cout));
  INC1 inc1_2 (.Cin(inc1_3_cout), .A(A[6]), .F(F[6]), .Cout(inc1_2_cout));
  INC1 inc1_3 (.Cin(inc1_4_cout), .A(A[5]), .F(F[5]), .Cout(inc1_3_cout));
  INC1 inc1_4 (.Cin(inc1_5_cout), .A(A[4]), .F(F[4]), .Cout(inc1_4_cout));
  INC1 inc1_5 (.Cin(inc1_6_cout), .A(A[3]), .F(F[3]), .Cout(inc1_5_cout));
  INC1 inc1_6 (.Cin(inc1_7_cout), .A(A[2]), .F(F[2]), .Cout(inc1_6_cout));
  INC1 inc1_7 (.Cin(inc1_8_cout), .A(A[1]), .F(F[1]), .Cout(inc1_7_cout));
  INC1 inc1_8 (.Cin(Cin), .A(A[0]), .F(F[0]), .Cout(inc1_8_cout));

  // Notes on the sheet:
  //   7..0
  //   7..0
endmodule

module INC16 (
  input  [15:0] A,
  input  Cin,
  output Cout,
  output [15:0] F
);

  wire inc8_2_cout;

  INC8 inc8_1 (.Cout(Cout), .Cin(inc8_2_cout), .A(A[15:8]), .F(F[15:8]));
  INC8 inc8_2 (.Cout(inc8_2_cout), .Cin(Cin), .A(A[7:0]), .F(F[7:0]));

  // Notes on the sheet:
  //   15..0
  //   15..0
endmodule

module MEM2x8 (
  input  [7:0] DIN,
  input  CLK,
  input  WR_RD,
  input  CS,
  input  A0,
  output [7:0] DOUT
);

  wire and_1_out, and_2_out, dc1_2_1_d0, dc1_2_1_d1, not_1_out;
  wire [7:0] controlled_buffer_1_out, reg8_ld_1_a7__0, reg8_ld_2_a7__0;

  not not_1 (not_1_out, WR_RD);
  DC1_2 dc1_2_1 (.En(CS), .X0(A0), .D0(dc1_2_1_d0), .D1(dc1_2_1_d1));
  REG8_LD reg8_ld_1 (.I7__0(DIN), .LD(and_1_out), .CLK(CLK), .A7__0(reg8_ld_1_a7__0));  // open: mr
  and and_1 (and_1_out, WR_RD, dc1_2_1_d0);
  assign controlled_buffer_1_out = dc1_2_1_d0 ? reg8_ld_1_a7__0 : 8'bz;  // Controlled_Buffer controlled_buffer_1
  assign DOUT = not_1_out ? controlled_buffer_1_out : 8'bz;  // Controlled_Buffer controlled_buffer_2
  REG8_LD reg8_ld_2 (.I7__0(DIN), .LD(and_2_out), .CLK(CLK), .A7__0(reg8_ld_2_a7__0));  // open: mr
  assign controlled_buffer_1_out = dc1_2_1_d1 ? reg8_ld_2_a7__0 : 8'bz;  // Controlled_Buffer controlled_buffer_3
  and and_2 (and_2_out, WR_RD, dc1_2_1_d1);

  // Notes on the sheet:
  //   __
endmodule

module MEM4x8 (
  input  [7:0] DIN,
  input  WR_RD,
  input  [1:0] A1__0,
  input  CS,
  input  CLK,
  output [7:0] DOUT
);

  wire dc1_2_1_d0, dc1_2_1_d1;

  DC1_2 dc1_2_1 (.En(CS), .X0(A1__0[1]), .D0(dc1_2_1_d0), .D1(dc1_2_1_d1));
  MEM2x8 mem2x8_1 (.DIN(DIN), .CLK(CLK), .CS(dc1_2_1_d0), .A0(A1__0[0]), .WR_RD(WR_RD), .DOUT(DOUT));
  MEM2x8 mem2x8_2 (.DIN(DIN), .CLK(CLK), .CS(dc1_2_1_d1), .A0(A1__0[0]), .WR_RD(WR_RD), .DOUT(DOUT));

  // Notes on the sheet:
  //   __
endmodule

module MEM8x8 (
  input  [7:0] DIN,
  input  WR_RD,
  input  [2:0] A2__0,
  input  CS,
  input  CLK,
  output [7:0] DOUT
);

  wire dc1_2_1_d0, dc1_2_1_d1;

  DC1_2 dc1_2_1 (.En(CS), .X0(A2__0[2]), .D0(dc1_2_1_d0), .D1(dc1_2_1_d1));
  MEM4x8 mem4x8_1 (.DIN(DIN), .WR_RD(WR_RD), .A1__0(A2__0[1:0]), .CS(dc1_2_1_d0), .CLK(CLK), .DOUT(DOUT));
  MEM4x8 mem4x8_2 (.DIN(DIN), .WR_RD(WR_RD), .A1__0(A2__0[1:0]), .CS(dc1_2_1_d1), .CLK(CLK), .DOUT(DOUT));

  // Notes on the sheet:
  //   __
endmodule

module MEM16x8 (
  input  [7:0] DIN,
  input  WR_RD,
  input  [3:0] A3__0,
  input  CS,
  input  CLK,
  output [7:0] DOUT
);

  wire dc1_2_1_d0, dc1_2_1_d1;

  DC1_2 dc1_2_1 (.En(CS), .X0(A3__0[3]), .D0(dc1_2_1_d0), .D1(dc1_2_1_d1));
  MEM8x8 mem8x8_1 (.DIN(DIN), .WR_RD(WR_RD), .A2__0(A3__0[2:0]), .CS(dc1_2_1_d0), .CLK(CLK), .DOUT(DOUT));
  MEM8x8 mem8x8_2 (.DIN(DIN), .WR_RD(WR_RD), .A2__0(A3__0[2:0]), .CS(dc1_2_1_d1), .CLK(CLK), .DOUT(DOUT));

  // Notes on the sheet:
  //   __
endmodule

module MEM32x8 (
  input  WR_RD,
  input  [4:0] A4__0,
  input  [7:0] DIN,
  input  CS,
  input  CLK,
  output [7:0] DOUT
);

  wire not_1_out;

  RAM #(.addrWidth(5), .bus("separate")) ram_1 (
    .addr(A4__0), .din(DIN), .data(DOUT), .str(WR_RD), .sel(CS), .clk(CLK), .ld(not_1_out), .clr(1'b0));
  not not_1 (not_1_out, WR_RD);

  // Notes on the sheet:
  //   __
endmodule

module MEM64x8 (
  input  WR_RD,
  input  [5:0] A5__0,
  input  [7:0] DIN,
  input  CS,
  input  CLK,
  output [7:0] DOUT
);

  wire not_1_out;

  RAM #(.addrWidth(6), .bus("separate")) ram_1 (
    .addr(A5__0), .din(DIN), .data(DOUT), .str(WR_RD), .sel(CS), .clk(CLK), .ld(not_1_out), .clr(1'b0));
  not not_1 (not_1_out, WR_RD);

  // Notes on the sheet:
  //   __
endmodule

module MEM128x8 (
  input  WR_RD,
  input  [6:0] A6__0,
  input  [7:0] DIN,
  input  CS,
  input  CLK,
  output [7:0] DOUT
);

  wire not_1_out;

  RAM #(.addrWidth(7), .bus("separate")) ram_1 (
    .addr(A6__0), .din(DIN), .data(DOUT), .str(WR_RD), .sel(CS), .clk(CLK), .ld(not_1_out), .clr(1'b0));
  not not_1 (not_1_out, WR_RD);

  // Notes on the sheet:
  //   __
endmodule

module MEM256x8 (
  input  WR_RD,
  input  [7:0] A7__0,
  input  [7:0] DIN,
  input  CS,
  input  CLK,
  output [7:0] DOUT
);

  wire not_1_out;

  RAM #(.bus("separate")) ram_1 (
    .addr(A7__0), .din(DIN), .data(DOUT), .str(WR_RD), .sel(CS), .clk(CLK), .ld(not_1_out), .clr(1'b0));
  not not_1 (not_1_out, WR_RD);

  // Notes on the sheet:
  //   __
endmodule

module MEM512x8 (
  input  WR_RD,
  input  [8:0] A8__0,
  input  [7:0] DIN,
  input  CS,
  input  CLK,
  output [7:0] DOUT
);

  wire not_1_out;

  RAM #(.addrWidth(9), .bus("separate")) ram_1 (
    .addr(A8__0), .din(DIN), .data(DOUT), .str(WR_RD), .sel(CS), .clk(CLK), .ld(not_1_out), .clr(1'b0));
  not not_1 (not_1_out, WR_RD);

  // Notes on the sheet:
  //   __
endmodule

module MEM1Kx8 (
  input  WR_RD,
  input  [9:0] A9__0,
  input  [7:0] DIN,
  input  CS,
  input  CLK,
  output [7:0] DOUT
);

  wire not_1_out;

  RAM #(.addrWidth(10), .bus("separate")) ram_1 (
    .addr(A9__0), .din(DIN), .data(DOUT), .str(WR_RD), .sel(CS), .clk(CLK), .ld(not_1_out), .clr(1'b0));
  not not_1 (not_1_out, WR_RD);

  // Notes on the sheet:
  //   __
endmodule

module MEM64Kx8 (
  input  WR_RD,
  input  [15:0] A15__0,
  input  [7:0] DIN,
  input  CS,
  input  CLK,
  output [7:0] DOUT
);

  wire not_1_out;

  RAM #(.addrWidth(16), .bus("separate")) ram_1 (
    .addr(A15__0), .din(DIN), .data(DOUT), .str(WR_RD), .sel(CS), .clk(CLK), .ld(not_1_out), .clr(1'b0));
  not not_1 (not_1_out, WR_RD);

  // Notes on the sheet:
  //   __
endmodule
