// Logisim project ETFExtended.circ as structural Verilog: 9 circuits, main circuit INTERRUPT_INTERFACE_4
module INTERRUPT_INTERFACE_4 (
  input  BTN_INTR0,
  input  BTN_INTR1,
  input  BTN_INTR2,
  input  BTN_INTR3,
  input  inta,
  input  [1:0] UEXT1__0,
  input  CLK,
  output [3:0] intr3__0
);

  wire and_1_out, and_2_out, and_3_out, and_4_out, D0, D1, D2, D3;

  DC2_4 dc2_4_1 (.En(inta), .X1__0(UEXT1__0), .D0(D0), .D1(D1), .D2(D2), .D3(D3));
  and and_1 (and_1_out, D0, ~BTN_INTR0);  // AND_Gate
  and and_2 (and_2_out, D1, ~BTN_INTR1);  // AND_Gate
  and and_3 (and_3_out, D2, ~BTN_INTR2);  // AND_Gate
  and and_4 (and_4_out, D3, ~BTN_INTR3);  // AND_Gate
  RSFF rsff_1 (.S(BTN_INTR0), .CLK(CLK), .R(and_1_out), .Q(intr3__0[0]));  // open: Sd, Rd, notQ
  RSFF rsff_2 (.S(BTN_INTR1), .CLK(CLK), .R(and_2_out), .Q(intr3__0[1]));  // open: Sd, Rd, notQ
  RSFF rsff_3 (.S(BTN_INTR2), .CLK(CLK), .R(and_3_out), .Q(intr3__0[2]));  // open: Sd, Rd, notQ
  RSFF rsff_4 (.S(BTN_INTR3), .CLK(CLK), .R(and_4_out), .Q(intr3__0[3]));  // open: Sd, Rd, notQ

  // Other names for the same wires on the sheet: intr0 = intr3__0[0]; intr1 = intr3__0[1]; intr2 = intr3__0[2];
  //   intr3 = intr3__0[3]
endmodule

module INTERRUPT_INTERFACE_8 (
  input  BTN_INTR0,
  input  BTN_INTR1,
  input  BTN_INTR2,
  input  BTN_INTR3,
  input  BTN_INTR4,
  input  BTN_INTR5,
  input  BTN_INTR6,
  input  BTN_INTR7,
  input  inta,
  input  [2:0] UEXT2__0,
  input  CLK,
  output [7:0] intr7__0
);

  wire and_1_out, and_2_out, and_3_out, and_4_out, and_5_out, and_6_out, and_7_out, and_8_out, D0, D1, D2,
       D3, D4, D5, D6, D7;

  DC3_8 dc3_8_1 (.En(inta), .X2__0(UEXT2__0), .D0(D0), .D1(D1), .D2(D2), .D3(D3), .D4(D4), .D5(D5), .D6(D6), .D7(D7));
  and and_1 (and_1_out, D0, ~BTN_INTR0);  // AND_Gate
  and and_2 (and_2_out, D1, ~BTN_INTR1);  // AND_Gate
  and and_3 (and_3_out, D2, ~BTN_INTR2);  // AND_Gate
  and and_4 (and_4_out, D3, ~BTN_INTR3);  // AND_Gate
  and and_5 (and_5_out, D4, ~BTN_INTR4);  // AND_Gate
  and and_6 (and_6_out, D5, ~BTN_INTR5);  // AND_Gate
  and and_7 (and_7_out, D6, ~BTN_INTR6);  // AND_Gate
  and and_8 (and_8_out, D7, ~BTN_INTR7);  // AND_Gate
  RSFF rsff_1 (.S(BTN_INTR0), .CLK(CLK), .R(and_1_out), .Q(intr7__0[0]));  // open: Sd, Rd, notQ
  RSFF rsff_2 (.S(BTN_INTR1), .CLK(CLK), .R(and_2_out), .Q(intr7__0[1]));  // open: Sd, Rd, notQ
  RSFF rsff_3 (.S(BTN_INTR2), .CLK(CLK), .R(and_3_out), .Q(intr7__0[2]));  // open: Sd, Rd, notQ
  RSFF rsff_4 (.S(BTN_INTR3), .CLK(CLK), .R(and_4_out), .Q(intr7__0[3]));  // open: Sd, Rd, notQ
  RSFF rsff_5 (.S(BTN_INTR4), .CLK(CLK), .R(and_5_out), .Q(intr7__0[4]));  // open: Sd, Rd, notQ
  RSFF rsff_6 (.S(BTN_INTR5), .CLK(CLK), .R(and_6_out), .Q(intr7__0[5]));  // open: Sd, Rd, notQ
  RSFF rsff_7 (.S(BTN_INTR6), .CLK(CLK), .R(and_7_out), .Q(intr7__0[6]));  // open: Sd, Rd, notQ
  RSFF rsff_8 (.S(BTN_INTR7), .CLK(CLK), .R(and_8_out), .Q(intr7__0[7]));  // open: Sd, Rd, notQ

  // Other names for the same wires on the sheet: intr0 = intr7__0[0]; intr1 = intr7__0[1]; intr2 = intr7__0[2];
  //   intr3 = intr7__0[3]; intr4 = intr7__0[4]; intr5 = intr7__0[5]; intr6 = intr7__0[6]; intr7 = intr7__0[7]
endmodule

module ROM16x24 (
  input  [3:0] A3__0,
  input  CS,
  output [23:0] DOUT
);

  ROM #(.addrWidth(4), .dataWidth(24)) rom_1 (.addr(A3__0), .data(DOUT), .sel(CS));
endmodule

module GPR8x16 (
  input  [15:0] DI15__0,
  input  [2:0] A2__0,
  input  WR,
  input  CLK,
  output [15:0] DO15__0
);

  wire and_1_out, and_2_out, and_3_out, and_4_out, and_5_out, and_6_out, and_7_out, and_8_out, CS0, CS1, CS2,
       CS3, CS4, CS5, CS6, CS7;
  wire [15:0] reg16_ld_1_a15__0, reg16_ld_2_a15__0, reg16_ld_3_a15__0, reg16_ld_4_a15__0, reg16_ld_5_a15__0,
       reg16_ld_6_a15__0, reg16_ld_7_a15__0, reg16_ld_8_a15__0;

  DC3_8 dc3_8_1 (
    .En(1'b1), .X2__0(A2__0), .D0(CS0), .D1(CS1), .D2(CS2), .D3(CS3), .D4(CS4), .D5(CS5), .D6(CS6), .D7(CS7));
  REG16_LD reg16_ld_1 (.I15__0(DI15__0), .LD(and_1_out), .CLK(CLK), .A15__0(reg16_ld_1_a15__0));  // open: mr
  assign DO15__0 = CS0 ? reg16_ld_1_a15__0 : 16'bz;  // Controlled_Buffer controlled_buffer_1
  REG16_LD reg16_ld_2 (.I15__0(DI15__0), .LD(and_2_out), .CLK(CLK), .A15__0(reg16_ld_2_a15__0));  // open: mr
  assign DO15__0 = CS1 ? reg16_ld_2_a15__0 : 16'bz;  // Controlled_Buffer controlled_buffer_2
  REG16_LD reg16_ld_3 (.I15__0(DI15__0), .LD(and_3_out), .CLK(CLK), .A15__0(reg16_ld_3_a15__0));  // open: mr
  assign DO15__0 = CS2 ? reg16_ld_3_a15__0 : 16'bz;  // Controlled_Buffer controlled_buffer_3
  REG16_LD reg16_ld_4 (.I15__0(DI15__0), .LD(and_4_out), .CLK(CLK), .A15__0(reg16_ld_4_a15__0));  // open: mr
  assign DO15__0 = CS3 ? reg16_ld_4_a15__0 : 16'bz;  // Controlled_Buffer controlled_buffer_4
  and and_1 (and_1_out, CS0, WR);
  and and_2 (and_2_out, CS1, WR);
  and and_3 (and_3_out, CS2, WR);
  and and_4 (and_4_out, CS3, WR);
  REG16_LD reg16_ld_5 (.I15__0(DI15__0), .LD(and_5_out), .CLK(CLK), .A15__0(reg16_ld_5_a15__0));  // open: mr
  and and_5 (and_5_out, CS4, WR);
  assign DO15__0 = CS4 ? reg16_ld_5_a15__0 : 16'bz;  // Controlled_Buffer controlled_buffer_5
  and and_6 (and_6_out, CS5, WR);
  REG16_LD reg16_ld_6 (.I15__0(DI15__0), .LD(and_6_out), .CLK(CLK), .A15__0(reg16_ld_6_a15__0));  // open: mr
  assign DO15__0 = CS5 ? reg16_ld_6_a15__0 : 16'bz;  // Controlled_Buffer controlled_buffer_6
  REG16_LD reg16_ld_7 (.I15__0(DI15__0), .LD(and_7_out), .CLK(CLK), .A15__0(reg16_ld_7_a15__0));  // open: mr
  and and_7 (and_7_out, CS6, WR);
  assign DO15__0 = CS6 ? reg16_ld_7_a15__0 : 16'bz;  // Controlled_Buffer controlled_buffer_7
  REG16_LD reg16_ld_8 (.I15__0(DI15__0), .LD(and_8_out), .CLK(CLK), .A15__0(reg16_ld_8_a15__0));  // open: mr
  and and_8 (and_8_out, CS7, WR);
  assign DO15__0 = CS7 ? reg16_ld_8_a15__0 : 16'bz;  // Controlled_Buffer controlled_buffer_8

  // Other names for the same wires on the sheet: inREG[15:0] = DI15__0; outREG[15:0] = DO15__0
endmodule

module ROM16x17 (
  input  [3:0] A3__0,
  input  CS,
  output [16:0] DOUT
);

  ROM #(.addrWidth(4), .dataWidth(17)) rom_1 (.addr(A3__0), .data(DOUT), .sel(CS));
endmodule

module ROM256x24 (
  input  [7:0] A7__0,
  input  CS,
  output [23:0] DOUT
);

  ROM #(.dataWidth(24)) rom_1 (.addr(A7__0), .data(DOUT), .sel(CS));
endmodule

module ROM256x28 (
  input  [7:0] A7__0,
  input  CS,
  output [27:0] DOUT
);

  ROM #(.dataWidth(28)) rom_1 (.addr(A7__0), .data(DOUT), .sel(CS));
endmodule

module ROM256x56 (
  input  [7:0] A7__0,
  input  CS,
  output [23:0] DOUT55__32,
  output [31:0] DOUT31__0
);

  ROM #(.dataWidth(24)) rom_1 (.addr(A7__0), .data(DOUT55__32), .sel(CS));
  ROM #(.dataWidth(32)) rom_2 (.addr(A7__0), .data(DOUT31__0), .sel(CS));
endmodule

module ROM256x64 (
  input  [7:0] A7__0,
  input  CS,
  output [31:0] DOUT63__32,
  output [31:0] DOUT31__0
);

  ROM #(.dataWidth(32)) rom_1 (.addr(A7__0), .data(DOUT63__32), .sel(CS));
  ROM #(.dataWidth(32)) rom_2 (.addr(A7__0), .data(DOUT31__0), .sel(CS));
endmodule
