// Logisim project ETFStudent.circ as structural Verilog: 4 circuits, main circuit REG32_LD_INC
module REG32_LD_INC (
);

  REG32_LD reg32_ld_1 ();  // open: I15__0, LD, mr, CLK, A15__0
endmodule

module REG32_LD (
  input  [31:0] I15__0,
  input  LD,
  input  mr,
  input  CLK,
  output [31:0] A15__0
);

  REG16_LD reg16_ld_1 (.I15__0(I15__0[31:16]), .LD(LD), .CLK(CLK), .A15__0(A15__0[31:16]), .mr(mr));
  REG16_LD reg16_ld_2 (.I15__0(I15__0[15:0]), .LD(LD), .CLK(CLK), .A15__0(A15__0[15:0]), .mr(mr));

  // Notes on the sheet:
  //   __
endmodule

module KMADR (
  input  immed,
  input  memdir,
  input  regdir,
  input  regindpom,
  output [7:0] Adr7__0
);

  assign Adr7__0 = immed ? 8'h2 : 8'bz;  // Controlled_Buffer controlled_buffer_1
  assign Adr7__0 = memdir ? 8'h3 : 8'bz;  // Controlled_Buffer controlled_buffer_2
  assign Adr7__0 = regdir ? 8'h4 : 8'bz;  // Controlled_Buffer controlled_buffer_3
  assign Adr7__0 = regindpom ? 8'h6 : 8'bz;  // Controlled_Buffer controlled_buffer_4
endmodule

module KMOPR (
  input  BUBBLE,
  input  LD,
  input  ST,
  input  ADD,
  input  SUB,
  input  BLSS,
  input  BGREU,
  input  JLEQ,
  input  JMP,
  input  JSR,
  input  RTS,
  input  RTI,
  input  PUSHGPR,
  input  POPGPR,
  input  HALT,
  output [7:0] Adr7__0
);

  assign Adr7__0 = LD ? 8'h2 : 8'bz;  // Controlled_Buffer controlled_buffer_1
  assign Adr7__0 = ST ? 8'h4 : 8'bz;  // Controlled_Buffer controlled_buffer_2
  assign Adr7__0 = ADD ? 8'h9 : 8'bz;  // Controlled_Buffer controlled_buffer_3
  assign Adr7__0 = SUB ? 8'hb : 8'bz;  // Controlled_Buffer controlled_buffer_4
  assign Adr7__0 = BLSS ? 8'hd : 8'bz;  // Controlled_Buffer controlled_buffer_5
  assign Adr7__0 = BGREU ? 8'hd : 8'bz;  // Controlled_Buffer controlled_buffer_6
  assign Adr7__0 = JLEQ ? 8'hf : 8'bz;  // Controlled_Buffer controlled_buffer_7
  assign Adr7__0 = JMP ? 8'h10 : 8'bz;  // Controlled_Buffer controlled_buffer_8
  assign Adr7__0 = JSR ? 8'h11 : 8'bz;  // Controlled_Buffer controlled_buffer_9
  assign Adr7__0 = RTS ? 8'h16 : 8'bz;  // Controlled_Buffer controlled_buffer_10
  assign Adr7__0 = RTI ? 8'h1d : 8'bz;  // Controlled_Buffer controlled_buffer_11
  assign Adr7__0 = PUSHGPR ? 8'h21 : 8'bz;  // Controlled_Buffer controlled_buffer_12
  assign Adr7__0 = POPGPR ? 8'h28 : 8'bz;  // Controlled_Buffer controlled_buffer_13
  assign Adr7__0 = HALT ? 8'h31 : 8'bz;  // Controlled_Buffer controlled_buffer_14
  assign Adr7__0 = BUBBLE ? 8'h33 : 8'bz;  // Controlled_Buffer controlled_buffer_15
endmodule
