// Logisim project ORT2Project.circ as structural Verilog: 7 circuits, main circuit COMPUTER
module COMPUTER (
);

  wire BTN_RST_out, CLK, pull_resistor_3_node, pull_resistor_6_node, ram_1_out_8, rst;
  wire [7:0] pull_resistor_4_node, ram_1_out_7;
  wire [15:0] pull_resistor_1_node;

  Button BTN_RST (.out(BTN_RST_out));
  Clock u_CLK (.out(CLK));
  RisingEdge risingedge_1 (.INPUT(BTN_RST_out), .CLK(CLK), .OUTPUT(rst));
  RAM ram_1 (
    .in_1(pull_resistor_1_node), .in_2(CLK), .in_3(pull_resistor_4_node), .in_4(pull_resistor_3_node),
    .in_5(pull_resistor_6_node), .in_6(rst), .out_7(ram_1_out_7), .out_8(ram_1_out_8));
  Pull_Resistor pull_resistor_1 (.node(pull_resistor_1_node));
  Pull_Resistor pull_resistor_2 (.node(ram_1_out_7));
  Pull_Resistor pull_resistor_3 (.node(pull_resistor_3_node));
  Pull_Resistor pull_resistor_4 (.node(pull_resistor_4_node));
  Pull_Resistor pull_resistor_5 (.node(ram_1_out_8));
  Pull_Resistor pull_resistor_6 (.node(pull_resistor_6_node));
  CPU cpu_1 (
    .in_1(rst), .in_2(CLK), .in_3(ram_1_out_8), .in_4(ram_1_out_7), .ABUS(pull_resistor_1_node),
    .DOUTBUS(pull_resistor_4_node), .out_7(pull_resistor_3_node), .out_8(pull_resistor_6_node));
endmodule

module CPU (
  input  in_1,
  input  in_2,
  input  in_3,
  input  [7:0] in_4,
  output [15:0] ABUS,
  output [7:0] DOUTBUS,
  output out_7,
  output out_8
);

  wire C;
  wire [2:0] CNT2__0;
  wire [3:0] common_1_phaseffbus;
  wire [7:0] A, ALU, B, common_1_addrbus, PSW, pull_resistor_7_node;
  wire [15:0] pull_resistor_5_node;
  wire [31:0] common_1_instrbus, pull_resistor_4_node, pull_resistor_6_node;

  COMMON common_1 (
    .CLK(in_2), .RST(in_1), .DIN(in_4), .CMEMBUS(pull_resistor_6_node), .MAR(ABUS), .MDR(DOUTBUS),
    .PHASEFFBUS(common_1_phaseffbus), .INSTRBUS(common_1_instrbus), .ADDRBUS(common_1_addrbus), .PSW(PSW),
    .CREGBUS(pull_resistor_4_node), .CFFBUS(pull_resistor_5_node), .CPSW(pull_resistor_7_node), .A7__0(A),
    .ALU7__0(ALU), .B7__0(B), .CNT2__0(CNT2__0), .ALUC(C));
  Pull_Resistor pull_resistor_1 (.node(common_1_instrbus));
  Pull_Resistor pull_resistor_2 (.node(common_1_phaseffbus));
  Pull_Resistor pull_resistor_3 (.node(common_1_addrbus));
  Pull_Resistor pull_resistor_4 (.node(pull_resistor_4_node));
  Pull_Resistor pull_resistor_5 (.node(pull_resistor_5_node));
  Pull_Resistor pull_resistor_6 (.node(pull_resistor_6_node));
  Pull_Resistor pull_resistor_7 (.node(pull_resistor_7_node));
  FETCH fetch_1 (
    .in_1(in_1), .in_2(in_2), .in_3(in_3), .PHASEFFBUS(common_1_phaseffbus), .INSTRBUS(common_1_instrbus),
    .ADDRBUS(common_1_addrbus), .PSW(PSW), .out_11(out_8), .CMEMBUS(pull_resistor_6_node),
    .CFFBUS(pull_resistor_5_node), .CREGBUS(pull_resistor_4_node));
  ADDR addr_1 (
    .in_1(in_1), .in_2(in_2), .in_3(in_3), .PHASEFFBUS(common_1_phaseffbus), .INSTRBUS(common_1_instrbus),
    .ADDRBUS(common_1_addrbus), .CMEMBUS(pull_resistor_6_node), .CFFBUS(pull_resistor_5_node),
    .CREGBUS(pull_resistor_4_node), .out_10(out_8));
  EXEC exec_1 (
    .in_1(in_1), .in_2(in_2), .in_3(in_3), .B(B), .PHASEFFBUS(common_1_phaseffbus),
    .INSTRBUS(common_1_instrbus), .ADDRBUS(common_1_addrbus), .PSW(PSW), .A7__0(A), .ALU7__0(ALU),
    .CMEMBUS(pull_resistor_6_node), .CFFBUS(pull_resistor_5_node), .CREGBUS(pull_resistor_4_node),
    .CPSW(pull_resistor_7_node), .rdMEM(out_8), .wrMEM(out_7), .CNT2__0(CNT2__0), .ALUC(C));

  // Other names for the same wires on the sheet: CLK = in_2; DIN7__0[7:0] = in_4; FCBUS = in_3; MAR[15:0] = ABUS;
  //   MDR[7:0] = DOUTBUS; RD = out_8; rst = in_1; WR = out_7

  // Notes on the sheet:
  //   out_7: pull=down
  //   out_8: pull=down
endmodule

module COMMON (
  input  CLK,
  input  RST,
  input  [7:0] DIN,
  input  [7:0] A7__0,
  input  [7:0] ALU7__0,
  input  [2:0] CNT2__0,
  input  ALUC,
  input  [31:0] CMEMBUS,
  input  [15:0] CFFBUS,
  input  [31:0] CREGBUS,
  input  [7:0] CPSW,
  output [15:0] MAR,
  output [7:0] MDR,
  output [3:0] PHASEFFBUS,
  output [31:0] INSTRBUS,
  output [7:0] ADDRBUS,
  output [7:0] PSW,
  output [7:0] B7__0
);

  wire ADRINST, adrinst1, adrinst2, adrinst3, adrinst_t, and_1_out, and_2_out, and_3_out, and_4_out,
       and_5_out, and_6_out, and_7_out, and_8_out, and_9_out, and_10_out, and_11_out, and_12_out, and_13_out,
       and_14_out, and_15_out, and_16_out, and_17_out, and_18_out, and_19_out, and_20_out, and_21_out,
       and_22_out, and_23_out, and_26_out, and_27_out, and_28_out, and_29_out, and_30_out, bezadrinst,
       branchinst, jmpinst, not_1_out, not_2_out, not_3_out, not_4_out, not_5_out, not_6_out, not_7_out,
       not_8_out, not_9_out, not_10_out, or_2_out, or_3_out, or_4_out, or_5_out, or_6_out, or_7_out,
       or_8_out, or_10_out, or_11_out, or_12_out;
  wire [3:0] IR19__16, mp4_4b_1_y;
  wire [7:0] cntI, cntJ, DWH, DWL, IR7__0, IR15__8, mp4_8b_1_y, mp8_8b_1_y, T1, T2;
  wire [7:4] IR23__16;
  wire [15:0] ADR15__0, GPR15__0, GPRDISP15__0, mp2_16b_1_out_5, mp2_16b_2_out_5, mp4_16b_1_y, mp8_16b_1_y,
       PC15__0, PCREL15__0, SP15__0, sub16_1_f;

  REG16_LD reg16_ld_1 (.I15__0(MAR), .LD(CREGBUS[11]), .CLK(CLK), .A15__0(ADR15__0));  // open: mr
  REG8_LD reg8_ld_1 (.I7__0(MDR), .LD(CREGBUS[6]), .CLK(CLK), .A7__0({IR23__16, IR19__16}));  // open: mr
  MP8_16b mp8_16b_1 (
    .En(1'b1), .S0(CMEMBUS[5]), .S1(CMEMBUS[6]), .S2(CREGBUS[12]), .I0(PC15__0), .I1({IR7__0, IR15__8}),
    .I2(GPRDISP15__0), .I3(SP15__0), .I4(ADR15__0), .I5(sub16_1_f), .Y(mp8_16b_1_y));  // open: I6, I7
  REG16_INC_LD reg16_inc_ld_1 (
    .I15__0(mp8_16b_1_y), .LD(CMEMBUS[0]), .INC(CMEMBUS[1]), .CLK(CLK), .A15__0(MAR));  // open: mr
  DC4_16 dc4_16_1 (
    .En(PSW[0]), .X3__0(IR23__16), .D0(bezadrinst), .D1(branchinst), .D2(jmpinst), .D3(adrinst1),
    .D4(adrinst2), .D6(adrinst3));  // open: D5, D7, D8, D9, D10, D11, D12, D13, D14, D15
  DC4_16 dc4_16_2 (
    .En(branchinst), .X3__0(IR19__16), .D0(INSTRBUS[8]), .D1(INSTRBUS[7]), .D2(INSTRBUS[9]));  // open: D3, D4, D5, D6, D7, D8, D9, D10, D11, D12, D13, D14, D15
  MP4_8b mp4_8b_1 (
    .S0(CREGBUS[1]), .S1(CREGBUS[2]), .I0(MDR), .I1(IR15__8), .I2(GPR15__0[7:0]), .Y(mp4_8b_1_y), .En(1'b1));  // open: I3
  REG8_LD reg8_ld_2 (.I7__0(mp4_8b_1_y), .LD(CREGBUS[0]), .CLK(CLK), .A7__0(B7__0));  // open: mr
  ADD16 add16_1 (.A({{12{IR15__8[7]}}, IR15__8[6:3]}), .B(GPR15__0), .F(GPRDISP15__0));  // open: C0, C16
  SUB16 sub16_1 (.A(MAR), .B(16'h1), .F(sub16_1_f));  // open: E0, E16
  REG8_LD reg8_ld_3 (.I7__0(MDR), .LD(CREGBUS[5]), .CLK(CLK), .A7__0(IR15__8));  // open: mr
  MP8_8b mp8_8b_1 (
    .En(1'b1), .S0(CMEMBUS[7]), .S1(CMEMBUS[8]), .S2(CMEMBUS[9]), .I0(DIN), .I1(A7__0), .I2(PC15__0[15:8]),
    .I3(PC15__0[7:0]), .I4(GPR15__0[15:8]), .I5(GPR15__0[7:0]), .I6(T1), .I7(T2), .Y(mp8_8b_1_y));
  REG8_LD reg8_ld_4 (.I7__0(mp8_8b_1_y), .LD(CMEMBUS[2]), .CLK(CLK), .A7__0(MDR));  // open: mr
  REG8_LD reg8_ld_5 (.I7__0(MDR), .LD(CREGBUS[4]), .CLK(CLK), .A7__0(IR7__0));  // open: mr
  DC4_16 dc4_16_3 (
    .En(bezadrinst), .X3__0(IR19__16), .D0(INSTRBUS[0]), .D1(INSTRBUS[1]), .D2(INSTRBUS[2]),
    .D3(INSTRBUS[4]), .D4(INSTRBUS[3]));  // open: D5, D6, D7, D8, D9, D10, D11, D12, D13, D14, D15
  DC4_16 dc4_16_4 (
    .En(jmpinst), .X3__0(IR19__16), .D0(INSTRBUS[5]), .D1(INSTRBUS[6]));  // open: D2, D3, D4, D5, D6, D7, D8, D9, D10, D11, D12, D13, D14, D15
  REG8_LD reg8_ld_6 (.I7__0(MDR), .LD(CREGBUS[8]), .CLK(CLK), .A7__0(DWH));  // open: mr
  ADD16 add16_2 (.A({{9{IR15__8[7]}}, IR15__8[6:0]}), .B(PC15__0), .F(PCREL15__0));  // open: C0, C16
  REG8_LD reg8_ld_7 (.I7__0(MDR), .LD(CREGBUS[7]), .CLK(CLK), .A7__0(DWL));  // open: mr
  MP4_16b mp4_16b_1 (
    .En(1'b1), .S0(CMEMBUS[13]), .S1(CMEMBUS[12]), .I0({IR7__0, IR15__8}), .I1(PCREL15__0), .I2({DWH, DWL}),
    .Y(mp4_16b_1_y));  // open: I3
  DC1_2 dc1_2_1 (.En(adrinst1), .X0(IR19__16[3]), .D0(INSTRBUS[12]), .D1(INSTRBUS[13]));
  DC1_2 dc1_2_2 (.En(adrinst2), .X0(IR19__16[3]), .D0(INSTRBUS[10]), .D1(INSTRBUS[11]));
  or or_1 (adrinst_t, adrinst1, adrinst3, adrinst2);
  DC1_2 dc1_2_3 (.En(adrinst3), .X0(IR19__16[3]), .D1(INSTRBUS[14]));  // open: D0
  DC3_8 dc3_8_1 (
    .En(adrinst_t), .X2__0(IR19__16[2:0]), .D0(ADDRBUS[0]), .D1(ADDRBUS[1]), .D2(ADDRBUS[2]), .D3(ADDRBUS[3]));  // open: D4, D5, D6, D7
  REG16 reg16_1 (
    .LD(RST), .A(16'hf000), .DEC(CMEMBUS[11]), .INC(CMEMBUS[10]), .CLK(CLK), .I(SP15__0));  // open: CL, SL, IL, SR, IR, Cout, Eout, mr
  not not_1 (not_1_out, RST);
  RSFF rsff_1 (.S(CFFBUS[0]), .CLK(CLK), .R(CFFBUS[1]), .Sd(not_1_out), .Q(PHASEFFBUS[0]));  // open: Rd, notQ
  MP2_16b mp2_16b_1 (.En(1'b1), .in_2(mp4_16b_1_y), .in_3(16'h1000), .S0(RST), .out_5(mp2_16b_1_out_5));
  REG16_INC_LD reg16_inc_ld_2 (
    .I15__0(mp2_16b_1_out_5), .LD(or_2_out), .INC(CMEMBUS[4]), .CLK(CLK), .A15__0(PC15__0));  // open: mr
  or or_2 (or_2_out, CMEMBUS[3], RST);
  RSFF rsff_2 (.S(CFFBUS[2]), .CLK(CLK), .R(CFFBUS[3]), .Rd(not_2_out), .Q(PHASEFFBUS[1]));  // open: Sd, notQ
  not not_2 (not_2_out, RST);
  MP4_4b mp4_4b_1 (
    .S0(CREGBUS[10]), .S1(CREGBUS[19]), .I0({1'b0, IR15__8[2:0]}), .I1({1'b0, CNT2__0}), .I2(4'b0000),
    .Y(mp4_4b_1_y));  // open: En, I3
  and and_1 (and_1_out, ~ALU7__0[7], B7__0[7], A7__0[7]);  // AND_Gate
  or or_3 (or_3_out, and_1_out, and_2_out);
  and and_2 (and_2_out, ALU7__0[7], ~B7__0[7], ~A7__0[7]);  // AND_Gate
  and and_3 (and_3_out, ~ALU7__0[7], ~B7__0[7], A7__0[7]);  // AND_Gate
  or or_4 (or_4_out, and_3_out, and_4_out);
  and and_4 (and_4_out, ALU7__0[7], B7__0[7], ~A7__0[7]);  // AND_Gate
  REG8 reg8_1 (
    .LD(CREGBUS[13]), .A(GPR15__0[7:0]), .DEC(CREGBUS[15]), .CLK(CLK), .I(cntI));  // open: CL, SL, IL, SR, IR, INC, Cout, Eout, mr
  nor nor_1 (INSTRBUS[29], cntI[7], cntI[6], cntI[5], cntI[4], cntI[3], cntI[2], cntI[1], cntI[0]);
  RSFF rsff_3 (.S(CFFBUS[4]), .CLK(CLK), .R(CFFBUS[5]), .Rd(not_3_out), .Q(PHASEFFBUS[2]));  // open: Sd, notQ
  not not_3 (not_3_out, RST);
  and and_5 (and_5_out, MDR[1], INSTRBUS[2]);
  and and_6 (and_6_out, ADRINST, and_7_out);
  and and_7 (and_7_out, ~A7__0[0], ~A7__0[1], ~A7__0[2], ~A7__0[3], ~A7__0[4], ~A7__0[5], ~A7__0[6], ~A7__0[7]);  // AND_Gate
  and and_8 (and_8_out, MDR[2], INSTRBUS[2]);
  and and_9 (and_9_out, ADRINST, A7__0[7]);
  and and_10 (and_10_out, MDR[3], INSTRBUS[2]);
  and and_11 (and_11_out, INSTRBUS[10], or_3_out);
  or or_5 (or_5_out, and_11_out, and_12_out);
  and and_12 (and_12_out, INSTRBUS[11], or_4_out);
  or or_6 (or_6_out, and_5_out, and_6_out);
  or or_7 (or_7_out, and_8_out, and_9_out);
  or or_8 (or_8_out, and_10_out, or_5_out);
  and and_13 (and_13_out, MDR[7], INSTRBUS[2]);
  MP2_16b mp2_16b_2 (
    .in_2({{9{A7__0[7]}}, A7__0[6:0]}), .in_3({DWH, DWL}), .S0(CREGBUS[9]), .out_5(mp2_16b_2_out_5));  // open: En
  GPR8x16 gpr8x16_1 (
    .DI15__0(mp2_16b_2_out_5), .A2__0(mp4_4b_1_y[2:0]), .WR(CREGBUS[3]), .CLK(CLK), .DO15__0(GPR15__0));
  REG8 reg8_2 (
    .LD(CREGBUS[14]), .A(GPR15__0[7:0]), .DEC(CREGBUS[16]), .CLK(CLK), .I(cntJ));  // open: CL, SL, IL, SR, IR, INC, Cout, Eout, mr
  or or_9 (ADRINST, INSTRBUS[12], INSTRBUS[10], INSTRBUS[11]);
  and and_14 (and_14_out, ~MDR[0], INSTRBUS[2], CPSW[6]);  // AND_Gate
  or or_10 (or_10_out, and_14_out, CPSW[0]);
  and and_15 (and_15_out, MDR[0], INSTRBUS[2], CPSW[6]);
  nor nor_2 (INSTRBUS[30], cntJ[7], cntJ[6], cntJ[5], cntJ[4], cntJ[3], cntJ[2], cntJ[1], ~cntJ[0]);  // NOR_Gate
  RSFF rsff_4 (.S(CFFBUS[6]), .CLK(CLK), .R(CFFBUS[7]), .Rd(not_4_out), .Q(PHASEFFBUS[3]));  // open: Sd, notQ
  not not_4 (not_4_out, RST);
  not not_5 (not_5_out, RST);
  RSFF rsff_5 (.S(and_15_out), .CLK(CLK), .R(or_10_out), .Sd(not_5_out), .Q(PSW[0]));  // open: Rd, notQ
  and and_16 (and_16_out, ~or_6_out, CPSW[3]);  // AND_Gate
  RSFF rsff_6 (.S(and_17_out), .CLK(CLK), .R(and_16_out), .Rd(not_6_out), .Q(PSW[1]));  // open: Sd, notQ
  and and_17 (and_17_out, or_6_out, CPSW[3]);
  not not_6 (not_6_out, RST);
  and and_18 (and_18_out, ~or_7_out, CPSW[2]);  // AND_Gate
  RSFF rsff_7 (.S(and_19_out), .CLK(CLK), .R(and_18_out), .Rd(not_7_out), .Q(PSW[2]));  // open: Sd, notQ
  and and_19 (and_19_out, or_7_out, CPSW[2]);
  not not_7 (not_7_out, RST);
  and and_20 (and_20_out, ~or_8_out, CPSW[5]);  // AND_Gate
  RSFF rsff_8 (.S(and_21_out), .CLK(CLK), .R(and_20_out), .Rd(not_8_out), .Q(PSW[3]));  // open: Sd, notQ
  and and_21 (and_21_out, or_8_out, CPSW[5]);
  not not_8 (not_8_out, RST);
  and and_22 (and_22_out, ~and_13_out, CPSW[1]);  // AND_Gate
  RSFF rsff_9 (.S(and_23_out), .CLK(CLK), .R(and_22_out), .Rd(not_9_out), .Q(PSW[7]));  // open: Sd, notQ
  not not_9 (not_9_out, RST);
  and and_23 (and_23_out, and_13_out, CPSW[1]);
  REG8_LD reg8_ld_8 (.I7__0(MDR), .LD(CREGBUS[17]), .CLK(CLK), .A7__0(T1));  // open: mr
  and and_24 (INSTRBUS[28], ~T1[7], T2[7]);  // AND_Gate
  and and_25 (INSTRBUS[27], T1[7], ~T2[7]);  // AND_Gate
  and and_26 (and_26_out, MDR[4], INSTRBUS[2]);
  and and_27 (and_27_out, INSTRBUS[10], ALUC);
  or or_11 (or_11_out, and_27_out, and_28_out);
  and and_28 (and_28_out, INSTRBUS[11], ALUC);
  REG8_LD reg8_ld_9 (.I7__0(MDR), .LD(CREGBUS[18]), .CLK(CLK), .A7__0(T2));  // open: mr
  or or_12 (or_12_out, and_26_out, or_11_out);
  and and_29 (and_29_out, ~or_12_out, CPSW[4]);  // AND_Gate
  and and_30 (and_30_out, or_12_out, CPSW[4]);
  SUB8 sub8_1 (.A(T1), .B(T2), .E8(INSTRBUS[31]));  // open: E0, F
  RSFF rsff_10 (.S(and_30_out), .CLK(CLK), .R(and_29_out), .Rd(not_10_out), .Q(PSW[4]));  // open: Sd, notQ
  not not_10 (not_10_out, RST);

  // Other names for the same wires on the sheet: A7 = A7__0[7]; immed = ADDRBUS[0]; memdir = ADDRBUS[1];
  //   regdir = ADDRBUS[2]; regindpom = ADDRBUS[3]; ALU7 = ALU7__0[7]; B7 = B7__0[7]; C = ALUC; stFETCH = CFFBUS[0];
  //   clFETCH = CFFBUS[1]; stADDR = CFFBUS[2]; clADDR = CFFBUS[3]; stEXEC = CFFBUS[4]; clEXEC = CFFBUS[5];
  //   stINTR = CFFBUS[6]; clINTR = CFFBUS[7]; ldMAR = CMEMBUS[0]; incMAR = CMEMBUS[1]; ldMDR = CMEMBUS[2];
  //   ldPC = CMEMBUS[3]; incPC = CMEMBUS[4]; mxMAR0 = CMEMBUS[5]; mxMAR1 = CMEMBUS[6]; mxMDR0 = CMEMBUS[7];
  //   mxMDR1 = CMEMBUS[8]; mxMDR2 = CMEMBUS[9]; incSP = CMEMBUS[10]; decSP = CMEMBUS[11]; mxPC1 = CMEMBUS[12];
  //   mxPC0 = CMEMBUS[13]; clPSWSTART = CPSW[0]; ldI = CPSW[1]; ldN = CPSW[2]; ldZ = CPSW[3]; ldC = CPSW[4];
  //   ldV = CPSW[5]; ldSTART = CPSW[6]; ldB = CREGBUS[0]; mxB0 = CREGBUS[1]; mxB1 = CREGBUS[2]; wrGPR = CREGBUS[3];
  //   ldIR7__0 = CREGBUS[4]; ldIR15__8 = CREGBUS[5]; ldIR23__16 = CREGBUS[6]; ldDWL = CREGBUS[7]; ldDWH = CREGBUS[8];
  //   mxGPR0 = CREGBUS[9]; mxGPRA0 = CREGBUS[10]; ldADR = CREGBUS[11]; mxMAR2 = CREGBUS[12]; ldI7__0 = CREGBUS[13];
  //   ldJ = CREGBUS[14]; decI = CREGBUS[15]; decJ = CREGBUS[16]; ldT1 = CREGBUS[17]; ldT2 = CREGBUS[18];
  //   mxGPRA1 = CREGBUS[19]; Din7__0[7:0] = DIN; HALT = INSTRBUS[0]; RTS = INSTRBUS[1]; RTI = INSTRBUS[2];
  //   POPGPR = INSTRBUS[3]; PUSHGPR = INSTRBUS[4]; JMP = INSTRBUS[5]; JSR = INSTRBUS[6]; BGREU = INSTRBUS[7];
  //   BLSS = INSTRBUS[8]; JLEQ = INSTRBUS[9]; ADD = INSTRBUS[10]; SUB = INSTRBUS[11]; LD = INSTRBUS[12];
  //   ST = INSTRBUS[13]; BUBBLE = INSTRBUS[14]; case1 = INSTRBUS[27]; case2 = INSTRBUS[28]; cntI0 = INSTRBUS[29];
  //   cntJ1 = INSTRBUS[30]; bse = INSTRBUS[31]; IR23__16[3:0] = IR19__16; MAR15__0[15:0] = MAR; MDR7__0[7:0] = MDR;
  //   FETCH = PHASEFFBUS[0]; ADDR = PHASEFFBUS[1]; EXEC = PHASEFFBUS[2]; INTR = PHASEFFBUS[3]; PSWSTART = PSW[0];
  //   PSWZ = PSW[1]; PSWN = PSW[2]; PSWV = PSW[3]; PSWC = PSW[4]; PSWI = PSW[7]

  // Notes on the sheet:
  //   MAR
  //   Sabirac
  //   Instrukcijski registar
  //   Pomocni registri
  //   Dekoderi za prepoznavanje instrukcije na osnovu sadrzaja registra IR23..16
  //   MDR
  //   PC
  //   Dekoderi za prepoznavanje nacina adresiranja
  //   SP
  //   FF za pokretanje FETCH, ADDR, EXEC i INTR faze izvršavanja instrukcije
  //   Registarski fajl
  //   Programska statusna reč (PSW)
endmodule

module FETCH (
  input  in_1,
  input  in_2,
  input  in_3,
  input  [3:0] PHASEFFBUS,
  input  [31:0] INSTRBUS,
  input  [7:0] ADDRBUS,
  input  [7:0] PSW,
  output [31:0] CMEMBUS,
  output [15:0] CFFBUS,
  output [31:0] CREGBUS,
  output out_11
);

  wire addr, addr2, addr3, and_1_out, and_2_out, and_3_out, and_5_out, and_6_out, and_7_out, and_8_out,
       and_9_out, and_10_out, and_11_out, and_12_out, and_13_out, and_14_out, and_15_out, bezadr1, bradr2,
       brbezadr1, brcnd, brgrinst, brjmp2, brjmp3, brnotfcbus, bruncnd, clFETCH, grinst, incPC, jmp2, jmp3,
       ldIR7__0, ldIR15__8, ldIR23__16, ldMAR, ldMDR, not_1_out, not_2_out, not_3_out, not_4_out, not_5_out,
       notPSWSandFETCH, or_4_out, or_5_out, or_6_out, or_7_out, or_10_out, or_11_out, or_12_out, rdMEM,
       stADDR, stEXEC;
  wire [3:0] rom256x24_1_dout_2;
  wire [7:0] reg8_inc_ld_1_a7__0, rom256x24_1_dout;
  wire [11:10] rom256x24_1_dout_3;

  or or_1 (bezadr1, INSTRBUS[1], INSTRBUS[2], INSTRBUS[0], INSTRBUS[3], INSTRBUS[4]);
  or or_2 (jmp2, INSTRBUS[8], INSTRBUS[7]);
  or or_3 (jmp3, INSTRBUS[9], INSTRBUS[5], INSTRBUS[6]);
  not not_1 (not_1_out, in_1);
  REG8_INC_LD reg8_inc_ld_1 (
    .I7__0(rom256x24_1_dout), .LD(or_5_out), .INC(not_2_out), .mr(not_1_out), .CLK(in_2),
    .A7__0(reg8_inc_ld_1_a7__0));
  or or_4 (or_4_out, ADDRBUS[2], ADDRBUS[3]);
  or or_5 (or_5_out, bruncnd, brcnd);
  not not_2 (not_2_out, or_5_out);
  ROM256x24 rom256x24_1 (
    .A7__0(reg8_inc_ld_1_a7__0), .CS(1'b1),
    .DOUT({rom256x24_1_dout, rom256x24_1_dout_2, rom256x24_1_dout_3, stEXEC, stADDR, clFETCH, ldIR7__0, ldIR15__8, ldIR23__16, ldMDR, rdMEM, incPC, ldMAR}));
  DC4_16 dc4_16_1 (
    .En(1'b1), .X3__0(rom256x24_1_dout_2), .D1(bruncnd), .D2(notPSWSandFETCH), .D3(brgrinst), .D4(brbezadr1),
    .D5(brjmp2), .D6(bradr2), .D7(brjmp3), .D8(brnotfcbus));  // open: D0, D9, D10, D11, D12, D13, D14, D15
  or or_6 (or_6_out, INSTRBUS[12], INSTRBUS[10], INSTRBUS[11]);
  or or_7 (or_7_out, ADDRBUS[0], or_4_out);
  and and_1 (and_1_out, or_6_out, or_7_out);
  and and_2 (and_2_out, or_4_out, INSTRBUS[13]);
  and and_3 (and_3_out, ADDRBUS[3], INSTRBUS[14]);
  and and_4 (addr3, ADDRBUS[1], addr);
  or or_8 (addr2, and_1_out, and_2_out, and_3_out);
  or or_9 (addr, INSTRBUS[12], INSTRBUS[13], INSTRBUS[14], INSTRBUS[10], INSTRBUS[11]);
  or or_10 (or_10_out, ADDRBUS[0], ADDRBUS[2]);
  not not_3 (not_3_out, PHASEFFBUS[0]);
  not not_4 (not_4_out, PSW[0]);
  and and_5 (and_5_out, ~bezadr1, ~jmp2, ~jmp3, ~addr);  // AND_Gate
  and and_6 (and_6_out, INSTRBUS[13], ADDRBUS[0]);
  and and_7 (and_7_out, ~addr3, ~addr2, addr);  // AND_Gate
  or or_11 (or_11_out, not_3_out, not_4_out);
  and and_8 (and_8_out, INSTRBUS[14], or_10_out);
  not not_5 (not_5_out, in_3);
  or or_12 (or_12_out, and_5_out, and_6_out, and_7_out);
  or or_13 (grinst, or_12_out, and_8_out);
  and and_9 (and_9_out, or_11_out, notPSWSandFETCH);
  and and_10 (and_10_out, brbezadr1, bezadr1);
  and and_11 (and_11_out, brgrinst, grinst);
  and and_12 (and_12_out, brjmp2, jmp2);
  and and_13 (and_13_out, bradr2, addr2);
  and and_14 (and_14_out, brjmp3, jmp3);
  and and_15 (and_15_out, brnotfcbus, not_5_out);
  or or_14 (brcnd, and_9_out, and_10_out, and_11_out, and_12_out, and_13_out, and_14_out, and_15_out);
  assign CMEMBUS[0] = ldMAR ? 1'b1 : 1'bz;  // Controlled_Buffer controlled_buffer_1
  assign CMEMBUS[2] = ldMDR ? 1'b1 : 1'bz;  // Controlled_Buffer controlled_buffer_2
  assign CMEMBUS[4] = incPC ? 1'b1 : 1'bz;  // Controlled_Buffer controlled_buffer_3
  assign CFFBUS[1] = clFETCH ? 1'b1 : 1'bz;  // Controlled_Buffer controlled_buffer_4
  assign CFFBUS[2] = stADDR ? 1'b1 : 1'bz;  // Controlled_Buffer controlled_buffer_5
  assign CFFBUS[4] = stEXEC ? 1'b1 : 1'bz;  // Controlled_Buffer controlled_buffer_6
  assign CREGBUS[4] = ldIR7__0 ? 1'b1 : 1'bz;  // Controlled_Buffer controlled_buffer_7
  assign CREGBUS[5] = ldIR15__8 ? 1'b1 : 1'bz;  // Controlled_Buffer controlled_buffer_8
  assign CREGBUS[6] = ldIR23__16 ? 1'b1 : 1'bz;  // Controlled_Buffer controlled_buffer_9
  assign out_11 = rdMEM ? 1'b1 : 1'bz;  // Controlled_Buffer controlled_buffer_10

  // Other names for the same wires on the sheet: immed = ADDRBUS[0]; memdir = ADDRBUS[1]; regdir = ADDRBUS[2];
  //   regindpom = ADDRBUS[3]; CLK = in_2; FCBUS = in_3; HALT = INSTRBUS[0]; RTS = INSTRBUS[1]; RTI = INSTRBUS[2];
  //   POPGPR = INSTRBUS[3]; PUSHGPR = INSTRBUS[4]; JMP = INSTRBUS[5]; JSR = INSTRBUS[6]; BGREU = INSTRBUS[7];
  //   BLSS = INSTRBUS[8]; JLEQ = INSTRBUS[9]; ADD = INSTRBUS[10]; SUB = INSTRBUS[11]; LD = INSTRBUS[12];
  //   ST = INSTRBUS[13]; BUBBLE = INSTRBUS[14]; FETCH = PHASEFFBUS[0]; PSWSTART = PSW[0]; rst = in_1

  // Notes on the sheet:
  //   Operaciona jedinica
  //   Upravljačka jedinica
endmodule

module ADDR (
  input  in_1,
  input  in_2,
  input  in_3,
  input  [3:0] PHASEFFBUS,
  input  [31:0] INSTRBUS,
  input  [7:0] ADDRBUS,
  output [31:0] CMEMBUS,
  output [15:0] CFFBUS,
  output [31:0] CREGBUS,
  output out_10
);

  wire and_1_out, and_2_out, and_3_out, bradr, brcnd, brnotADDR, brnotfcbus, brSTORE, bruncnd, clADDR, ldB,
       ldMAR, ldMDR, mxB0, mxB1, mxMAR0, mxMAR1, not_1_out, not_2_out, not_3_out, not_4_out, or_1_out, rdMEM,
       stEXEC;
  wire [7:0] kmadr_1_adr7__0, mp2_8b_1_out_5, reg8_inc_ld_1_a7__0;
  wire [27:10] rom256x28_1_dout;

  not not_1 (not_1_out, in_1);
  KMADR kmadr_1 (
    .immed(ADDRBUS[0]), .memdir(ADDRBUS[1]), .regdir(ADDRBUS[2]), .regindpom(ADDRBUS[3]),
    .Adr7__0(kmadr_1_adr7__0));
  MP2_8b mp2_8b_1 (
    .in_2(rom256x28_1_dout[27:20]), .in_3(kmadr_1_adr7__0), .S0(bradr), .out_5(mp2_8b_1_out_5), .En(1'b1));
  REG8_INC_LD reg8_inc_ld_1 (
    .I7__0(mp2_8b_1_out_5), .LD(or_1_out), .INC(not_2_out), .mr(not_1_out), .CLK(in_2),
    .A7__0(reg8_inc_ld_1_a7__0));
  not not_2 (not_2_out, or_1_out);
  ROM256x28 rom256x28_1 (
    .A7__0(reg8_inc_ld_1_a7__0), .CS(1'b1),
    .DOUT({rom256x28_1_dout, stEXEC, clADDR, ldMDR, rdMEM, mxMAR1, mxB1, mxMAR0, ldMAR, mxB0, ldB}));
  or or_1 (or_1_out, bruncnd, brcnd, bradr);
  DC4_16 dc4_16_1 (
    .En(1'b1), .X3__0(rom256x28_1_dout[19:16]), .D1(bruncnd), .D2(brnotADDR), .D3(brSTORE), .D4(brnotfcbus),
    .D5(bradr));  // open: D0, D6, D7, D8, D9, D10, D11, D12, D13, D14, D15
  not not_3 (not_3_out, PHASEFFBUS[1]);
  not not_4 (not_4_out, in_3);
  and and_1 (and_1_out, not_3_out, brnotADDR);
  and and_2 (and_2_out, INSTRBUS[13], brSTORE);
  and and_3 (and_3_out, brnotfcbus, not_4_out);
  or or_2 (brcnd, and_1_out, and_2_out, and_3_out);
  assign CMEMBUS[0] = ldMAR ? 1'b1 : 1'bz;  // Controlled_Buffer controlled_buffer_1
  assign CMEMBUS[2] = ldMDR ? 1'b1 : 1'bz;  // Controlled_Buffer controlled_buffer_2
  assign CMEMBUS[5] = mxMAR0 ? 1'b1 : 1'bz;  // Controlled_Buffer controlled_buffer_3
  assign CMEMBUS[6] = mxMAR1 ? 1'b1 : 1'bz;  // Controlled_Buffer controlled_buffer_4
  assign CFFBUS[3] = clADDR ? 1'b1 : 1'bz;  // Controlled_Buffer controlled_buffer_5
  assign CFFBUS[4] = stEXEC ? 1'b1 : 1'bz;  // Controlled_Buffer controlled_buffer_6
  assign CREGBUS[0] = ldB ? 1'b1 : 1'bz;  // Controlled_Buffer controlled_buffer_7
  assign CREGBUS[1] = mxB0 ? 1'b1 : 1'bz;  // Controlled_Buffer controlled_buffer_8
  assign CREGBUS[2] = mxB1 ? 1'b1 : 1'bz;  // Controlled_Buffer controlled_buffer_9
  assign out_10 = rdMEM ? 1'b1 : 1'bz;  // Controlled_Buffer controlled_buffer_10

  // Other names for the same wires on the sheet: immed = ADDRBUS[0]; memdir = ADDRBUS[1]; regdir = ADDRBUS[2];
  //   regindpom = ADDRBUS[3]; CLK = in_2; FCBUS = in_3; ST = INSTRBUS[13]; ADDR = PHASEFFBUS[1]; rst = in_1

  // Notes on the sheet:
  //   Operaciona jedinica
  //   Upravljacka jedinica
endmodule

module EXEC (
  input  in_1,
  input  in_2,
  input  in_3,
  input  [7:0] B,
  input  [3:0] PHASEFFBUS,
  input  [31:0] INSTRBUS,
  input  [7:0] ADDRBUS,
  input  [7:0] PSW,
  output [7:0] A7__0,
  output [7:0] ALU7__0,
  output [2:0] CNT2__0,
  output ALUC,
  output [31:0] CMEMBUS,
  output [15:0] CFFBUS,
  output [31:0] CREGBUS,
  output [7:0] CPSW,
  output rdMEM,
  output wrMEM
);

  wire add_t, and_2_out, and_3_out, and_4_out, and_5_out, and_6_out, and_7_out, and_8_out, and_9_out,
       and_10_out, and_11_out, and_12_out, and_13_out, and_14_out, and_15_out, brbse, brcase1, brcase2,
       brcnd, brcntI0, brcntJ1, brnotbrorjmp, brnotCNT0, brnotCNT7, brnotEXEC, brnotFCBUS, bropr, brorjmp,
       brregdir, bruncnd, clEXEC, clPSWSTART, CNT0, CNT7, decCNT, decI, decJ, decSP, incCNT, incMAR, incSP,
       ldA, ldADR, ldC, ldCNT, ldDWH, ldDWL, ldI, ldI7__0, ldJ, ldMAR, ldMDR, ldN, ldPC, ldSTART, ldT1, ldT2,
       ldV, ldZ, mxA0, mxCNT0, mxGPR0, mxGPRA0, mxGPRA1, mxMAR0, mxMAR1, mxMAR2, mxMDR0, mxMDR1, mxMDR2,
       mxPC0, mxPC1, not_1_out, not_2_out, not_3_out, not_4_out, not_5_out, not_6_out, not_7_out, not_8_out,
       not_9_out, or_1_out, or_2_out, or_4_out, or_6_out, rdMEM_t, stINTR, sub_t, wrGPR, wrMEM_t, xor_1_out;
  wire [3:0] mp2_4b_1_y;
  wire [7:0] kmopr_1_adr7__0, mp2_8b_1_out_5, mp2_8b_2_out_5, reg8_inc_ld_1_a7__0;
  wire [31:14] rom256x64_1_dout63__32;

  MP2_8b mp2_8b_1 (.in_2(B), .in_3(ALU7__0), .S0(mxA0), .out_5(mp2_8b_1_out_5));  // open: En
  not not_1 (not_1_out, in_1);
  REG8_LD reg8_ld_1 (.I7__0(mp2_8b_1_out_5), .LD(ldA), .CLK(in_2), .A7__0(A7__0), .mr(not_1_out));
  not not_2 (not_2_out, in_1);
  DC4_16 dc4_16_1 (
    .En(1'b1), .X3__0(rom256x64_1_dout63__32[23:20]), .D1(bruncnd), .D2(brnotEXEC), .D3(brregdir),
    .D4(brnotbrorjmp), .D5(brnotCNT0), .D6(brnotCNT7), .D7(brnotFCBUS), .D8(bropr), .D9(brcase1),
    .D10(brcase2), .D11(brcntI0), .D12(brcntJ1), .D13(brbse));  // open: D0, D14, D15
  KMOPR kmopr_1 (
    .LD(INSTRBUS[12]), .ST(INSTRBUS[13]), .ADD(INSTRBUS[10]), .SUB(INSTRBUS[11]), .BLSS(INSTRBUS[8]),
    .BGREU(INSTRBUS[7]), .JLEQ(INSTRBUS[9]), .JMP(INSTRBUS[5]), .JSR(INSTRBUS[6]), .RTS(INSTRBUS[1]),
    .RTI(INSTRBUS[2]), .PUSHGPR(INSTRBUS[4]), .POPGPR(INSTRBUS[3]), .HALT(INSTRBUS[0]),
    .Adr7__0(kmopr_1_adr7__0), .BUBBLE(INSTRBUS[14]));
  MP2_8b mp2_8b_2 (
    .in_2(rom256x64_1_dout63__32[31:24]), .in_3(kmopr_1_adr7__0), .S0(bropr), .out_5(mp2_8b_2_out_5),
    .En(1'b1));
  REG8_INC_LD reg8_inc_ld_1 (
    .I7__0(mp2_8b_2_out_5), .LD(or_1_out), .INC(not_3_out), .mr(not_2_out), .CLK(in_2),
    .A7__0(reg8_inc_ld_1_a7__0));
  not not_3 (not_3_out, or_1_out);
  ROM256x64 rom256x64_1 (
    .A7__0(reg8_inc_ld_1_a7__0), .CS(1'b1),
    .DOUT63__32({rom256x64_1_dout63__32, mxGPRA1, decI, decJ, ldT2, incMAR, ldT1, ldJ, mxMAR2, ldI7__0, ldADR, clEXEC, stINTR, ldI, clPSWSTART}),
    .DOUT31__0({mxGPR0, incCNT, mxCNT0, decCNT, mxGPRA0, mxMDR2, ldCNT, ldSTART, mxPC1, ldDWH, ldDWL, rdMEM_t, incSP, mxMDR1, decSP, ldMAR, mxMAR1, mxMAR0, ldPC, mxPC0, sub_t, ldC, ldV, add_t, mxA0, wrGPR, wrMEM_t, ldMDR, mxMDR0, ldZ, ldN, ldA}));
  ALU8_ADD_SUB alu8_add_sub_1 (.Cin(1'b0), .A(A7__0), .B(B), .add(add_t), .sub(sub_t), .F(ALU7__0), .Cout(ALUC));
  or or_1 (or_1_out, bruncnd, brcnd, bropr);
  MP2_4b mp2_4b_1 (.in_2(4'b0111), .in_3(4'b0000), .S0(mxCNT0), .Y(mp2_4b_1_y));  // open: En
  REG3m_DEC_INC_LD reg3m_dec_inc_ld_1 (
    .I2__0(mp2_4b_1_y[2:0]), .LD(ldCNT), .DEC(decCNT), .INC(incCNT), .CLK(in_2), .Ein(decCNT), .Cin(incCNT),
    .A2__0(CNT2__0));  // open: mr, Eout, Cout
  nor nor_1 (CNT0, CNT2__0[0], CNT2__0[1], CNT2__0[2]);
  and and_1 (CNT7, CNT2__0[0], CNT2__0[1], CNT2__0[2]);
  xor xor_1 (xor_1_out, PSW[2], PSW[3]);
  or or_2 (or_2_out, xor_1_out, PSW[1]);
  not not_4 (not_4_out, PSW[4]);
  and and_2 (and_2_out, xor_1_out, INSTRBUS[8]);
  and and_3 (and_3_out, or_2_out, INSTRBUS[9]);
  and and_4 (and_4_out, not_4_out, INSTRBUS[7]);
  or or_3 (brorjmp, and_2_out, and_3_out, and_4_out);
  not not_5 (not_5_out, PHASEFFBUS[2]);
  not not_6 (not_6_out, CNT0);
  not not_7 (not_7_out, brorjmp);
  not not_8 (not_8_out, in_3);
  not not_9 (not_9_out, CNT7);
  and and_5 (and_5_out, not_5_out, brnotEXEC);
  and and_6 (and_6_out, not_6_out, brnotCNT0);
  and and_7 (and_7_out, ADDRBUS[2], brregdir);
  and and_8 (and_8_out, not_7_out, brnotbrorjmp);
  and and_9 (and_9_out, not_8_out, brnotFCBUS);
  and and_10 (and_10_out, not_9_out, brnotCNT7);
  and and_11 (and_11_out, INSTRBUS[27], brcase1);
  and and_12 (and_12_out, INSTRBUS[28], brcase2);
  and and_13 (and_13_out, INSTRBUS[29], brcntI0);
  and and_14 (and_14_out, INSTRBUS[30], brcntJ1);
  and and_15 (and_15_out, INSTRBUS[31], brbse);
  or or_4 (or_4_out, and_5_out, and_6_out, and_7_out, and_8_out, and_9_out, and_10_out);
  or or_5 (brcnd, or_4_out, or_6_out);
  or or_6 (or_6_out, and_11_out, and_12_out, and_13_out, and_14_out, and_15_out);
  assign CMEMBUS[1] = incMAR ? 1'b1 : 1'bz;  // Controlled_Buffer controlled_buffer_1
  assign CREGBUS[11] = ldADR ? 1'b1 : 1'bz;  // Controlled_Buffer controlled_buffer_2
  assign CREGBUS[13] = ldI7__0 ? 1'b1 : 1'bz;  // Controlled_Buffer controlled_buffer_3
  assign CREGBUS[15] = decI ? 1'b1 : 1'bz;  // Controlled_Buffer controlled_buffer_4
  assign CREGBUS[17] = ldT1 ? 1'b1 : 1'bz;  // Controlled_Buffer controlled_buffer_5
  assign CREGBUS[18] = ldT2 ? 1'b1 : 1'bz;  // Controlled_Buffer controlled_buffer_6
  assign CPSW[0] = clPSWSTART ? 1'b1 : 1'bz;  // Controlled_Buffer controlled_buffer_7
  assign CPSW[1] = ldI ? 1'b1 : 1'bz;  // Controlled_Buffer controlled_buffer_8
  assign CPSW[2] = ldN ? 1'b1 : 1'bz;  // Controlled_Buffer controlled_buffer_9
  assign CPSW[3] = ldZ ? 1'b1 : 1'bz;  // Controlled_Buffer controlled_buffer_10
  assign CPSW[4] = ldC ? 1'b1 : 1'bz;  // Controlled_Buffer controlled_buffer_11
  assign CPSW[5] = ldV ? 1'b1 : 1'bz;  // Controlled_Buffer controlled_buffer_12
  assign CPSW[6] = ldSTART ? 1'b1 : 1'bz;  // Controlled_Buffer controlled_buffer_13
  assign CMEMBUS[0] = ldMAR ? 1'b1 : 1'bz;  // Controlled_Buffer controlled_buffer_14
  assign CMEMBUS[2] = ldMDR ? 1'b1 : 1'bz;  // Controlled_Buffer controlled_buffer_15
  assign CMEMBUS[3] = ldPC ? 1'b1 : 1'bz;  // Controlled_Buffer controlled_buffer_16
  assign CMEMBUS[5] = mxMAR0 ? 1'b1 : 1'bz;  // Controlled_Buffer controlled_buffer_17
  assign CMEMBUS[6] = mxMAR1 ? 1'b1 : 1'bz;  // Controlled_Buffer controlled_buffer_18
  assign CMEMBUS[7] = mxMDR0 ? 1'b1 : 1'bz;  // Controlled_Buffer controlled_buffer_19
  assign CMEMBUS[8] = mxMDR1 ? 1'b1 : 1'bz;  // Controlled_Buffer controlled_buffer_20
  assign CMEMBUS[9] = mxMDR2 ? 1'b1 : 1'bz;  // Controlled_Buffer controlled_buffer_21
  assign CMEMBUS[10] = incSP ? 1'b1 : 1'bz;  // Controlled_Buffer controlled_buffer_22
  assign CMEMBUS[11] = decSP ? 1'b1 : 1'bz;  // Controlled_Buffer controlled_buffer_23
  assign CMEMBUS[12] = mxPC1 ? 1'b1 : 1'bz;  // Controlled_Buffer controlled_buffer_24
  assign CMEMBUS[13] = mxPC0 ? 1'b1 : 1'bz;  // Controlled_Buffer controlled_buffer_25
  assign CFFBUS[5] = clEXEC ? 1'b1 : 1'bz;  // Controlled_Buffer controlled_buffer_26
  assign CFFBUS[6] = stINTR ? 1'b1 : 1'bz;  // Controlled_Buffer controlled_buffer_27
  assign CREGBUS[3] = wrGPR ? 1'b1 : 1'bz;  // Controlled_Buffer controlled_buffer_28
  assign CREGBUS[7] = ldDWL ? 1'b1 : 1'bz;  // Controlled_Buffer controlled_buffer_29
  assign CREGBUS[8] = ldDWH ? 1'b1 : 1'bz;  // Controlled_Buffer controlled_buffer_30
  assign CREGBUS[9] = mxGPR0 ? 1'b1 : 1'bz;  // Controlled_Buffer controlled_buffer_31
  assign CREGBUS[10] = mxGPRA0 ? 1'b1 : 1'bz;  // Controlled_Buffer controlled_buffer_32
  assign CREGBUS[12] = mxMAR2 ? 1'b1 : 1'bz;  // Controlled_Buffer controlled_buffer_33
  assign CREGBUS[14] = ldJ ? 1'b1 : 1'bz;  // Controlled_Buffer controlled_buffer_34
  assign CREGBUS[16] = decJ ? 1'b1 : 1'bz;  // Controlled_Buffer controlled_buffer_35
  assign CREGBUS[19] = mxGPRA1 ? 1'b1 : 1'bz;  // Controlled_Buffer controlled_buffer_36
  assign rdMEM = rdMEM_t ? 1'b1 : 1'bz;  // Controlled_Buffer controlled_buffer_37
  assign wrMEM = wrMEM_t ? 1'b1 : 1'bz;  // Controlled_Buffer controlled_buffer_38

  assign CFFBUS[0] = CFFBUS[6];

  // Other names for the same wires on the sheet: regdir = ADDRBUS[2]; B7__0[7:0] = B; C = ALUC; CLK = in_2;
  //   FCBUS = in_3; HALT = INSTRBUS[0]; RTS = INSTRBUS[1]; RTI = INSTRBUS[2]; POPGPR = INSTRBUS[3];
  //   PUSHGPR = INSTRBUS[4]; JMP = INSTRBUS[5]; JSR = INSTRBUS[6]; BGREU = INSTRBUS[7]; BLSS = INSTRBUS[8];
  //   JLEQ = INSTRBUS[9]; ADD = INSTRBUS[10]; SUB = INSTRBUS[11]; LD = INSTRBUS[12]; ST = INSTRBUS[13];
  //   BUBBLE = INSTRBUS[14]; case1 = INSTRBUS[27]; case2 = INSTRBUS[28]; cntI0 = INSTRBUS[29]; cntJ1 = INSTRBUS[30];
  //   bse = INSTRBUS[31]; EXEC = PHASEFFBUS[2]; PSWZ = PSW[1]; PSWN = PSW[2]; PSWV = PSW[3]; PSWC = PSW[4];
  //   rst = in_1

  // Notes on the sheet:
  //   CPSW: pull=down
  //   Akumulator
  //   Operaciona jedinica
  //   Upravljacka jedinica
  //   Upravljacka jedinica
  //   ALU
  //   Uslov za skok
endmodule

module RAM (
  input  [15:0] in_1,
  input  in_2,
  input  [7:0] in_3,
  input  in_4,
  input  in_5,
  input  in_6,
  output [7:0] out_7,
  output out_8
);

  wire and_1_out, and_2_out, CNT0, LDCNT, not_1_out, not_2_out, not_3_out, notCNT0, or_1_out, rsff_2_q, sl,
       xor_1_out;
  wire [3:0] CNT, LFSR;

  RSFF rsff_1 (.S(in_6), .CLK(in_2), .R(1'b0), .Q(sl));  // open: Sd, Rd, notQ
  or or_1 (or_1_out, in_4, in_5);
  REG4_LD_SL_SR reg4_ld_sl_sr_1 (
    .I3__0(4'b1111), .LD(in_6), .IR(1'b0), .SR(1'b0), .IL(xor_1_out), .SL(sl), .CLK(in_2), .A3__0(LFSR));  // open: mr
  RisingEdge risingedge_1 (.INPUT(or_1_out), .CLK(in_2), .OUTPUT(LDCNT));
  MEM64Kx8 mem64kx8_1 (.WR_RD(in_4), .A15__0(in_1), .DIN(in_3), .CS(1'b1), .CLK(in_2), .DOUT(out_7));
  xor xor_1 (xor_1_out, LFSR[2], LFSR[3]);
  and and_1 (and_1_out, CNT0, not_1_out);
  not not_1 (not_1_out, LDCNT);
  RSFF rsff_2 (.S(LDCNT), .CLK(in_2), .R(and_1_out), .Rd(not_2_out), .Q(rsff_2_q));  // open: Sd, notQ
  not not_2 (not_2_out, in_6);
  and and_2 (and_2_out, rsff_2_q, CNT0);
  REG4m_DEC_LD reg4m_dec_ld_1 (
    .I3__0(LFSR), .LD(LDCNT), .Ein(notCNT0), .DEC(notCNT0), .CLK(in_2), .A3__0(CNT));  // open: Eout, mr
  or or_2 (notCNT0, CNT[0], CNT[1], CNT[2], CNT[3]);
  RSFF rsff_3 (.S(and_2_out), .CLK(in_2), .R(out_8), .Rd(not_3_out), .Q(out_8));  // open: Sd, notQ
  not not_3 (not_3_out, in_6);
  not not_4 (CNT0, notCNT0);

  // Other names for the same wires on the sheet: ADR[15:0] = in_1; CLK = in_2; DIN[7:0] = in_3; DOUT[7:0] = out_7;
  //   fc = out_8; RDMEM = in_5; rst = in_6; WRMEM = in_4

  // Notes on the sheet:
  //   Random broj predstavlja vreme pristupa memoriji
  //   Brojac za generisanje random broja 
  //   Jedinica za generisanje function complete (fc) signala
  //   Brojac za dekrementiranje random broja
endmodule
